// Logisim project 7400-lib-td4.circ as structural Verilog: 4 circuits, main circuit main
module main (
);

  _74173 u_74173_1 ();  // open: _1____M, _2____N, _3___1Q, _4___2Q, _5___3Q, _6___4Q, _7__CLK, _8__GND, _16__Vcc, _15_CLR, _14__1D, _13___2D, _12___3D, _11___4D, _10___2G, _9___1G
  _74283 u_74283_1 ();  // open: _1__S2, _2__B2, _3__A2, _4__S1, _5__A1, _6__B1, _7__Cin, _8__GND, _16__Vcc, _15__B3, _14__A3, _13__S3, _12__A4, _11__B4, _10__S4, _9__Cout
  _74173 u_74173_2 ();  // open: _1____M, _2____N, _3___1Q, _4___2Q, _5___3Q, _6___4Q, _7__CLK, _8__GND, _16__Vcc, _15_CLR, _14__1D, _13___2D, _12___3D, _11___4D, _10___2G, _9___1G
  _74283 u_74283_2 ();  // open: _1__S2, _2__B2, _3__A2, _4__S1, _5__A1, _6__B1, _7__Cin, _8__GND, _16__Vcc, _15__B3, _14__A3, _13__S3, _12__A4, _11__B4, _10__S4, _9__Cout
  _74259 u_74259_1 ();  // open: _1__S0, _2__S1, _3__S2, _4__Q0, _5__Q1, _6__Q2, _7__Q3, _8__GND, _16__Vcc, _15__CLR, _14__G, _13__D, _12__Q7, _11__Q6, _10__Q5, _9__Q4
  _74259 u_74259_2 ();  // open: _1__S0, _2__S1, _3__S2, _4__Q0, _5__Q1, _6__Q2, _7__Q3, _8__GND, _16__Vcc, _15__CLR, _14__G, _13__D, _12__Q7, _11__Q6, _10__Q5, _9__Q4

  // Notes on the sheet:
  //   4bit D-type register
  //   with tristate output
  //   4bit D-type register 
  //   4bit D-type register 
  //   4bit D-type register 
  //   with tristate output
  //   with tristate output
  //   with tristate output
  //   4-bit binary
  //   4-bit binary
  //   4-bit binary
  //   full adder
  //   full adder
  //   full adder
  //   4bit binary
  //   full adder
  //   8bit addressable latches
  //   8bit addressble latches
  //   8bit addressble latches
  //   8bit addressble latches
endmodule

module _74173 (
  input  _1____M,
  input  _16__Vcc,
  input  _2____N,
  input  _15_CLR,
  input  _14__1D,
  input  _13___2D,
  input  _12___3D,
  input  _11___4D,
  input  _7__CLK,
  input  _10___2G,
  input  _8__GND,
  input  _9___1G,
  output _3___1Q,
  output _4___2Q,
  output _5___3Q,
  output _6___4Q
);

  wire and_1_out, and_2_out, d_ff_1_q, d_ff_2_q, d_ff_3_q, d_ff_4_q, multiplexer_1_out, multiplexer_2_out,
       multiplexer_3_out, multiplexer_4_out;

  and and_1 (and_1_out, ~_1____M, ~_2____N);  // AND_Gate
  Multiplexer #(.enable("false")) multiplexer_1 (
    .in0(d_ff_1_q), .in1(_14__1D), .out(multiplexer_1_out), .sel(and_2_out));
  Multiplexer #(.enable("false")) multiplexer_2 (
    .in0(d_ff_2_q), .in1(_13___2D), .out(multiplexer_2_out), .sel(and_2_out));
  Multiplexer #(.enable("false")) multiplexer_3 (
    .in0(d_ff_3_q), .in1(_12___3D), .out(multiplexer_3_out), .sel(and_2_out));
  Multiplexer #(.enable("false")) multiplexer_4 (
    .in0(d_ff_4_q), .in1(_11___4D), .out(multiplexer_4_out), .sel(and_2_out));
  D_Flip_Flop d_ff_1 (
    .clk(_7__CLK), .D(multiplexer_1_out), .Q(d_ff_1_q), .preset(1'b0), .en(and_2_out), .reset(_15_CLR));  // open: Qn
  D_Flip_Flop d_ff_2 (
    .clk(_7__CLK), .D(multiplexer_2_out), .Q(d_ff_2_q), .preset(1'b0), .en(and_2_out), .reset(_15_CLR));  // open: Qn
  D_Flip_Flop d_ff_3 (
    .clk(_7__CLK), .D(multiplexer_3_out), .Q(d_ff_3_q), .preset(1'b0), .en(and_2_out), .reset(_15_CLR));  // open: Qn
  D_Flip_Flop d_ff_4 (
    .clk(_7__CLK), .D(multiplexer_4_out), .Q(d_ff_4_q), .preset(1'b0), .en(and_2_out), .reset(_15_CLR));  // open: Qn
  and and_2 (and_2_out, ~_10___2G, ~_9___1G);  // AND_Gate
  assign _3___1Q = and_1_out ? d_ff_1_q : 1'bz;  // Controlled_Buffer controlled_buffer_1
  assign _4___2Q = and_1_out ? d_ff_2_q : 1'bz;  // Controlled_Buffer controlled_buffer_2
  assign _5___3Q = and_1_out ? d_ff_3_q : 1'bz;  // Controlled_Buffer controlled_buffer_3
  assign _6___4Q = and_1_out ? d_ff_4_q : 1'bz;  // Controlled_Buffer controlled_buffer_4

  // Notes on the sheet:
  //   74173: 4-Bit D-Type Registers With 3-State Outputs
endmodule

module _74283 (
  input  _16__Vcc,
  input  _2__B2,
  input  _15__B3,
  input  _3__A2,
  input  _14__A3,
  input  _5__A1,
  input  _12__A4,
  input  _6__B1,
  input  _11__B4,
  input  _7__Cin,
  input  _8__GND,
  output _1__S2,
  output _4__S1,
  output _13__S3,
  output _10__S4,
  output _9__Cout
);

  // _7483 7483_1: pin names not known; wires that end beside it: _8__GND, _3__A2, _4__S1, _2__B2, _5__A1, _1__S2, _6__B1, _15__B3, _7__Cin, _14__A3, _9__Cout, _13__S3, _10__S4, _12__A4, _11__B4, _16__Vcc

  // Notes on the sheet:
  //   74283: 4-bit full adder
endmodule

module _74259 (
  input  _1__S0,
  input  _16__Vcc,
  input  _2__S1,
  input  _15__CLR,
  input  _3__S2,
  input  _14__G,
  input  _13__D,
  input  _8__GND,
  output _4__Q0,
  output _5__Q1,
  output _12__Q7,
  output _6__Q2,
  output _11__Q6,
  output _7__Q3,
  output _10__Q5,
  output _9__Q4
);

  wire decoder_1_out0, decoder_1_out1, decoder_1_out2, decoder_1_out3, decoder_1_out4, decoder_1_out5,
       decoder_1_out6, decoder_1_out7, not_1_out;

  Decoder #(.select(3), .disabled(0)) decoder_1 (
    .out0(decoder_1_out0), .out1(decoder_1_out1), .out2(decoder_1_out2), .out3(decoder_1_out3),
    .out4(decoder_1_out4), .out5(decoder_1_out5), .out6(decoder_1_out6), .out7(decoder_1_out7),
    .sel({_3__S2, _2__S1, _1__S0}), .en(_14__G));
  D_Flip_Flop d_ff_1 (
    .clk(decoder_1_out0), .D(_13__D), .Q(_4__Q0), .preset(1'b0), .en(1'b1), .reset(not_1_out));  // open: Qn
  not not_1 (not_1_out, _15__CLR);
  D_Flip_Flop d_ff_2 (
    .clk(decoder_1_out1), .D(_13__D), .Q(_5__Q1), .preset(1'b0), .en(1'b1), .reset(not_1_out));  // open: Qn
  D_Flip_Flop d_ff_3 (
    .clk(decoder_1_out2), .D(_13__D), .Q(_6__Q2), .preset(1'b0), .en(1'b1), .reset(not_1_out));  // open: Qn
  D_Flip_Flop d_ff_4 (
    .clk(decoder_1_out3), .D(_13__D), .Q(_7__Q3), .preset(1'b0), .en(1'b1), .reset(not_1_out));  // open: Qn
  D_Flip_Flop d_ff_5 (
    .clk(decoder_1_out4), .D(_13__D), .Q(_9__Q4), .preset(1'b0), .en(1'b1), .reset(not_1_out));  // open: Qn
  D_Flip_Flop d_ff_6 (
    .clk(decoder_1_out5), .D(_13__D), .Q(_10__Q5), .preset(1'b0), .en(1'b1), .reset(not_1_out));  // open: Qn
  D_Flip_Flop d_ff_7 (
    .clk(decoder_1_out6), .D(_13__D), .Q(_11__Q6), .preset(1'b0), .en(1'b1), .reset(not_1_out));  // open: Qn
  D_Flip_Flop d_ff_8 (
    .clk(decoder_1_out7), .D(_13__D), .Q(_12__Q7), .preset(1'b0), .en(1'b1), .reset(not_1_out));  // open: Qn

  // Notes on the sheet:
  //   8-bit addressable latches
endmodule
