// Logisim project CPU298.circ as structural Verilog: 27 circuits, main circuit System
module System (
);

  wire and_1_out, Clock_out, decoder_1_out0, decoder_1_out1, decoder_1_out2, decoder_1_out3,
       n298_core_1_navma, n298_core_1_read, n298_core_1_trap, n298_core_1_write, not_1_out, Reset, undriven,
       undriven_2;
  wire [7:0] n298_core_1_dataout;
  wire [15:0] n298_core_1_addressout;

  Clock Clock (.out(Clock_out));
  Button button_1 (.out(Reset));
  _298_CORE u_298_core_1 (
    .Reset(Reset), .DataOut(n298_core_1_dataout), .DataIn(n298_core_1_dataout), .Read(n298_core_1_read),
    .AddressOut(n298_core_1_addressout), .Write(n298_core_1_write), .CLK(Clock_out),
    .nAVMA(n298_core_1_navma), .in_1(undriven), .in_2(undriven_2), .Trap(n298_core_1_trap));  // open: S0, S1, Q, E, StateUpdate
  // Probe on n298_core_1_addressout
  // Probe on n298_core_1_dataout
  Pull_Resistor pull_resistor_1 (.node(n298_core_1_dataout));
  Pull_Resistor pull_resistor_2 (.node(n298_core_1_addressout));
  Decoder #(.select(2), .disabled(0)) decoder_1 (
    .out0(decoder_1_out0), .out1(decoder_1_out1), .out2(decoder_1_out2), .out3(decoder_1_out3),
    .sel(n298_core_1_addressout[15:14]), .en(not_1_out));
  not not_1 (not_1_out, n298_core_1_navma);
  RAM #(.addrWidth(14)) ram_1 (
    .addr(n298_core_1_addressout[13:0]), .data(n298_core_1_dataout), .sel(decoder_1_out0),
    .clk(n298_core_1_write), .ld(n298_core_1_read), .clr(1'b0));
  RAM #(.addrWidth(14)) ram_2 (
    .addr(n298_core_1_addressout[13:0]), .data(n298_core_1_dataout), .sel(decoder_1_out1),
    .clk(n298_core_1_write), .ld(n298_core_1_read), .clr(1'b0));
  RAM #(.addrWidth(14)) ram_3 (
    .addr(n298_core_1_addressout[13:0]), .data(n298_core_1_dataout), .sel(decoder_1_out2),
    .clk(n298_core_1_write), .ld(n298_core_1_read), .clr(1'b0));
  and and_1 (and_1_out, n298_core_1_read, decoder_1_out3);
  ROM #(.addrWidth(14)) rom_1 (.addr(n298_core_1_addressout[13:0]), .data(n298_core_1_dataout), .sel(and_1_out));

  // Notes on the sheet:
  //   ADDR Decoder
  //   RAM0 0000-3FFF
  //   RAM1 4000-7FFF
  //   RAM2 8000-BFFF
  //   ROM0 C000-FFFF
  //   contents of rom_1 (hex, n*v repeats v):
  //   68 11 0 2 f8 9 c0 ee fb fb c0 ee fb fb 2 0 ee fe 7c 0 f 0 a5 8 e5 fb d6 9 fe e9 ff 48 65 6c 6c 6f 0
  //   6e 48 65 6c 6c 6f 21*0 8 5a 28 0 80 17*0 76 553*0 34 413*0 fe 231*0 76 2553*0 f8 aa 8478*0 6e 4062*0
  //   c0
endmodule

module _298_CORE (
  input  in_1,
  input  in_2,
  input  [7:0] DataIn,
  input  CLK,
  input  Reset,
  output [7:0] DataOut,
  output [15:0] AddressOut,
  output Write,
  output Read,
  output nAVMA,
  output StateUpdate,
  output S1,
  output S0,
  output Trap,
  output Q,
  output E
);

  wire and_1_out, C, CLK_t, ManualCLK, nand_1_out, nand_2_out, nand_4_out, nor_1_out, nor_2_out, nor_3_out,
       not_1_out, not_2_out, not_3_out, not_4_out, not_5_out, not_6_out, not_7_out, nRST, Resume,
       sr_latch_1_ny;
  wire [1:0] sequencer_1_exbuscontrol;
  wire [2:0] executer_1_flagregisterout;
  wire [5:0] sequencer_1_aluop;
  wire [7:0] buffer_1_out, executer_1_dataout, sequencer_1_dataout, sequencer_1_executercontrol,
       sequencer_1_op;
  wire [11:0] sequencer_1_step_monitor;
  wire [15:0] executer_1_addrout;

  // Probe on sequencer_1_op
  F0 f0_1 (.OP(sequencer_1_op), .F0(Trap));
  not not_1 (not_1_out, Resume);
  Executer executer_1 (
    .DataOut(executer_1_dataout), .FlagRegisterOut(executer_1_flagregisterout), .E(E),
    .AddrOut(executer_1_addrout), .DataIn(sequencer_1_dataout), .RegisterCtrl(sequencer_1_executercontrol),
    .STEP(sequencer_1_step_monitor), .ALUOP(sequencer_1_aluop), .Q(Q), .CLK(ManualCLK), .Resume(Resume),
    .C(C), .CLK_monitor(CLK_t), .FlagSelector(in_1), .nINT(in_2));
  // Probe on sequencer_1_executercontrol
  // Probe on sequencer_1_aluop
  Sequencer sequencer_1 (
    .FlagIn(executer_1_flagregisterout), .nReset(nRST), .DataIn(buffer_1_out),
    .ExecuterControl(sequencer_1_executercontrol), .ExBusControl(sequencer_1_exbuscontrol),
    .STEP_Monitor(sequencer_1_step_monitor), .DataOut(sequencer_1_dataout), .StateUpdate(StateUpdate),
    .ALUOP(sequencer_1_aluop), .Q(Q), .C(C), .E(E), .CLK_Monitor(CLK_t), .OP(sequencer_1_op), .State_1(S1),
    .State_0(S0));  // open: Jcc_OP, nDO_JUMP, StateClock, LoadOpeCode, μROMAddrCLK
  and and_1 (and_1_out, Trap, ~C, E);  // AND_Gate
  nand nand_1 (nand_1_out, not_1_out, nRST);
  // Probe on executer_1_dataout
  // Probe on executer_1_addrout
  not not_2 (not_2_out, ManualCLK);
  not not_3 (not_3_out, and_1_out);
  not not_4 (not_4_out, nand_1_out);
  D_FF16 d_ff16_1 (.In(executer_1_addrout), .Out(AddressOut), .CLK(Q));
  not not_5 (not_5_out, sequencer_1_exbuscontrol[0]);
  Multiplexer #(.disabled(0), .enable("false")) multiplexer_1 (
    .in0(not_2_out), .in1(CLK), .out(CLK_t), .sel(sr_latch_1_ny));
  SR_Latch sr_latch_1 (.nR(not_3_out), .nS(not_4_out), .nY(sr_latch_1_ny));
  D_FF8 d_ff8_1 (.In(executer_1_dataout), .CLK(Q), .nOE(not_6_out), .Out(DataOut));
  not not_6 (not_6_out, nor_1_out);
  nor nor_1 (nor_1_out, nor_2_out, nand_2_out);
  nor nor_2 (nor_2_out, Q, C);
  nand nand_2 (nand_2_out, not_5_out, sequencer_1_exbuscontrol[1]);
  not not_7 (not_7_out, nand_2_out);
  nor nor_3 (nor_3_out, not_5_out, sequencer_1_exbuscontrol[1]);
  assign buffer_1_out = DataIn;  // Buffer buffer_1, 8 bits wide
  // Probe on DataIn
  // Probe on DataOut
  // Probe on AddressOut
  nand nand_3 (Write, Q, not_7_out);
  nand nand_4 (nand_4_out, nor_3_out, C);
  not not_8 (Read, nand_4_out);
  nor nor_4 (nAVMA, not_7_out, nor_3_out);
  CLK_GEN clk_gen_1 (.CLK(CLK_t), .Reset(Reset), .nRST(nRST), .T1(Q), .T2(C), .T3(E));

  // Notes on the sheet:
  //   Reset: pull=up
  //   574
  //   OE付き D-FF 
  //   Q↑でラッチQ|Cの間出力イネーブル
  //   DataBus_In_Buffer
  //   HCT245
  //   DataBus_Out
  //   AddressBus
  //   バス使用予告信号
endmodule

module F0 (
  input  [7:0] OP,
  output F0
);

  wire and_1_out, and_3_out, not_1_out, not_2_out, not_3_out, not_4_out;

  not not_1 (not_1_out, OP[4]);
  not not_2 (not_2_out, OP[5]);
  not not_3 (not_3_out, OP[6]);
  not not_4 (not_4_out, OP[7]);
  and and_1 (and_1_out, OP[0], OP[1], OP[2], OP[3]);
  and and_2 (F0, and_1_out, and_3_out);
  and and_3 (and_3_out, not_1_out, not_2_out, not_3_out, not_4_out);
endmodule

module Sequencer (
  input  [7:0] DataIn,
  input  CLK_Monitor,
  input  nReset,
  input  Q,
  input  C,
  input  E,
  input  [2:0] FlagIn,
  output [11:0] STEP_Monitor,
  output [7:0] OP,
  output LoadOpeCode,
  output \μROMAddrCLK ,
  output [7:0] ExecuterControl,
  output [5:0] ALUOP,
  output StateUpdate,
  output [1:0] ExBusControl,
  output StateClock,
  output [7:0] DataOut,
  output State_1,
  output State_0,
  output Jcc_OP,
  output nDO_JUMP
);

  wire and_1_out, and_5_out, multiplexer_1_out, nC, nE, nor_1_out, nor_2_out, nor_3_out, not_4_out,
       not_5_out, not_6_out, not_7_out, not_8_out, nQ, nROM_A0, ResetFlag_qn, State_Bit0_qn, State_Bit1_qn;
  wire [3:0] OP_Code;
  wire [7:0] controlled_buffer_1_out, IR_q;
  wire [11:0] urom8_1_step_mon;
  wire [15:0] urom8_1_ctrlsignal;

  LED led_1 (.in(CLK_Monitor));
  not not_1 (nQ, Q);
  not not_2 (nC, C);
  not not_3 (nE, E);
  // Probe on {DataIn[7:4], OP_Code}
  and and_1 (and_1_out, nROM_A0, State_0);
  not not_4 (not_4_out, nReset);
  Register IR (.D({DataIn[7:4], OP_Code}), .en(and_1_out), .Q(IR_q), .clk(nQ));  // open: clr
  D_Flip_Flop State_Bit1 (
    .clk(StateClock), .D(State_0), .Q(State_1), .Qn(State_Bit1_qn), .reset(not_4_out));  // open: preset, en
  not not_5 (not_5_out, nReset);
  assign controlled_buffer_1_out = not_6_out ? {7'b1110000, State_0} : 8'bz;  // Controlled_Buffer controlled_buffer_1
  assign controlled_buffer_1_out = nor_1_out ? IR_q : 8'bz;  // Controlled_Buffer controlled_buffer_2
  not not_6 (not_6_out, nor_1_out);
  nor nor_1 (nor_1_out, State_0, State_Bit1_qn);
  D_Flip_Flop State_Bit0 (
    .clk(StateClock), .D(State_Bit0_qn), .Q(State_0), .Qn(State_Bit0_qn), .reset(not_5_out));  // open: preset, en
  // Probe on controlled_buffer_1_out
  and and_2 (LoadOpeCode, Q, ~nor_2_out);  // AND_Gate
  nor nor_2 (nor_2_out, ResetFlag_qn, StateUpdate);
  D_Flip_Flop ResetFlag (.clk(nC), .D(1'b1), .Qn(ResetFlag_qn), .reset(not_7_out));  // open: Q, preset, en
  not not_7 (not_7_out, nReset);
  and and_3 (StateClock, StateUpdate, Q);
  uROM8 urom8_1 (
    .OpeCode(controlled_buffer_1_out), .Load(LoadOpeCode), .Update(C), .nQ(nQ),
    .CtrlSignal(urom8_1_ctrlsignal), .STEP_MON(urom8_1_step_mon));
  nor nor_3 (nor_3_out, FlagIn[0], FlagIn[1]);
  and and_4 (StateUpdate, ExBusControl[0], ExBusControl[1]);
  Multiplexer #(.select(2), .disabled(0), .enable("false")) multiplexer_1 (
    .in0(FlagIn[0]), .in1(FlagIn[1]), .in2(nor_3_out), .in3(FlagIn[2]), .out(multiplexer_1_out),
    .sel(DataIn[2:1]));
  Register #(.width(16)) Ctrl_signal_register (
    .D(urom8_1_ctrlsignal), .Q({ExBusControl, ALUOP, ExecuterControl}), .clk(nE), .clr(not_8_out));  // open: en
  not not_8 (not_8_out, nReset);
  and and_5 (and_5_out, DataIn[5], DataIn[6], DataIn[7]);
  Register #(.width(12)) register_1 (.D(urom8_1_step_mon), .Q({OP, STEP_Monitor[3:0]}), .clk(nE));  // open: en, clr
  D_Flip_Flop d_ff_1 (.clk(nE), .D(urom8_1_step_mon[0]), .Qn(nROM_A0));  // open: Q, preset, en, reset
  and and_6 (Jcc_OP, ~DataIn[3], ~DataIn[4], and_5_out);  // AND_Gate
  xor xor_1 (nDO_JUMP, DataIn[0], multiplexer_1_out);
  Multiplexer #(.width(4), .disabled(0), .enable("false")) multiplexer_2 (
    .in0(DataIn[3:0]), .in1({3'b111, nDO_JUMP}), .out(OP_Code), .sel(Jcc_OP));

  assign DataOut = DataIn;
  assign STEP_Monitor[11:4] = OP;
  assign \μROMAddrCLK  = C;

  // Other names for the same wires on the sheet: CF = FlagIn[0]; ZF = FlagIn[1]; SF = FlagIn[2]

  // Notes on the sheet:
  //   nReset: pull=up
  //   Fetch
  //   377
  //   実行ステージ以外のときは0xEx
  //   2to1x4 157
  //   OP Selector
  //   Execute
  //   μROM_IDX
  //   00:Reset
  //   01:Fetch
  //   State Control
  //   10:Execute
  //   C↑で変化する
  //   4tp1 153
  //   HCT273 AsyncReset
  //   プロトタイプはGAL16で
  //   Jcc Detector
  //   HCT74
  //   2to1x4 157
  //   条件Jump
  //   分岐するか
endmodule

module Executer (
  input  CLK_monitor,
  input  Q,
  input  C,
  input  E,
  input  [7:0] DataIn,
  input  FlagSelector,
  input  [11:0] STEP,
  input  nINT,
  input  [5:0] ALUOP,
  input  [7:0] RegisterCtrl,
  output [2:0] FlagRegisterOut,
  output [7:0] DataOut,
  output [15:0] AddrOut,
  output CLK,
  output Resume
);

  wire and_1_out, decoder_1_out0, decoder_1_out1, decoder_1_out2, decoder_1_out3, decoder_1_out4,
       decoder_1_out5, decoder_1_out6, decoder_1_out7, inc_dec16_1_dec, inc_dec16_1_inc, mux4to1x8_1_i0,
       mux4to1x8_1_i1, mux4to1x8_1_i2, mux4to1x8_1_i3, mux4to1x16_1_i0, mux4to1x16_1_i1, mux4to1x16_1_i2,
       mux4to1x16_1_i3, not_1_out, not_2_out, opgen_1_fl;
  wire [1:0] alu_1_carry_2;
  wire [2:0] Flag_q, multiplexer_2_out, register_1_q;
  wire [3:0] opgen_1_op;
  wire [7:0] Acc_q, alu_1_loutmon, H_q, L_q, multiplexer_1_out, mux4to1x8_1_y, W_q;
  wire [8:0] opgen_1_opout;
  wire [15:0] mux4to1x16_1_y, PC_q, X_q, Y_q;

  LED led_1 (.in(CLK_monitor));
  not not_1 (not_1_out, Q);
  // Probe on DataIn
  // Probe on STEP
  // Probe on RegisterCtrl[7:5]
  and and_1 (and_1_out, not_1_out, C);
  Decoder #(.select(3), .disabled(0)) decoder_1 (
    .out0(decoder_1_out0), .out1(decoder_1_out1), .out2(decoder_1_out2), .out3(decoder_1_out3),
    .out4(decoder_1_out4), .out5(decoder_1_out5), .out6(decoder_1_out6), .out7(decoder_1_out7),
    .sel(RegisterCtrl[7:5]), .en(and_1_out));
  Register Acc (.D(DataOut), .Q(Acc_q), .clk(decoder_1_out0));  // open: en, clr
  Register W (.D(DataOut), .Q(W_q), .clk(decoder_1_out1));  // open: en, clr
  Register H (.D(DataOut), .Q(H_q), .clk(decoder_1_out2));  // open: en, clr
  Register L (.D(DataOut), .Q(L_q), .clk(decoder_1_out3));  // open: en, clr
  Register #(.width(16)) X (.D(AddrOut), .Q(X_q), .clk(decoder_1_out4));  // open: en, clr
  Register #(.width(16)) Y (.D(AddrOut), .Q(Y_q), .clk(decoder_1_out5));  // open: en, clr
  Register #(.width(16)) PC (.D(AddrOut), .Q(PC_q), .clk(decoder_1_out6));  // open: en, clr
  Multiplexer #(.width(8), .disabled(0), .enable("false")) multiplexer_1 (
    .in0(Acc_q), .in1(W_q), .out(multiplexer_1_out), .sel(RegisterCtrl[2]));
  MUX4to1x16 mux4to1x16_1 (
    .D0({H_q, L_q}), .D1(X_q), .D2(Y_q), .D3(PC_q), .Sel(RegisterCtrl[4:3]), .Y(mux4to1x16_1_y),
    .I0(mux4to1x16_1_i0), .I1(mux4to1x16_1_i1), .I2(mux4to1x16_1_i2), .I3(mux4to1x16_1_i3));
  // Probe on AddrOut
  MUX4to1x8 mux4to1x8_1 (
    .D0(W_q), .D1(DataIn), .D2(AddrOut[15:8]), .D3(AddrOut[7:0]), .Sel(RegisterCtrl[1:0]), .Y(mux4to1x8_1_y),
    .I0(mux4to1x8_1_i0), .I1(mux4to1x8_1_i1), .I2(mux4to1x8_1_i2), .I3(mux4to1x8_1_i3));
  // Probe on mux4to1x16_1_y
  // Probe on ALUOP[3:0]
  // Probe on multiplexer_1_out
  // Probe on mux4to1x8_1_y
  // Probe on DataOut
  // Probe on ALUOP[5:4]
  OPGen opgen_1 (.OPin(ALUOP[3:0]), .OP(opgen_1_op), .OpOut(opgen_1_opout), .FL(opgen_1_fl));
  // Probe on opgen_1_op
  // Probe on alu_1_loutmon
  INC_DEC16 inc_dec16_1 (
    .IN(mux4to1x16_1_y), .OUT(AddrOut), .INC(inc_dec16_1_inc), .DEC(inc_dec16_1_dec), .Addr(ALUOP[5:4]),
    .Offset8(multiplexer_1_out));
  // Probe on {DataOut[7], alu_1_carry_2}
  ALU alu_1 (
    .A(multiplexer_1_out), .Carry_2(alu_1_carry_2[0]), .ALU_OUT(DataOut), .ZF(alu_1_carry_2[1]),
    .B(mux4to1x8_1_y), .LOutMon(alu_1_loutmon), .OpIn(opgen_1_opout), .Carry(FlagRegisterOut[0]));
  Register #(.width(3)) Flag (.D({DataOut[7], alu_1_carry_2}), .en(opgen_1_fl), .Q(Flag_q), .clk(E));  // open: clr
  not not_2 (not_2_out, C);
  Button ManualClock (.out(CLK));
  Button u_Resume (.out(Resume));
  Register #(.width(3)) register_1 (.D(Flag_q), .en(nINT), .Q(register_1_q), .clk(not_2_out));  // open: clr
  Register #(.width(3)) register_2 (.D(multiplexer_2_out), .Q(FlagRegisterOut), .clk(not_2_out));  // open: en, clr
  Multiplexer #(.width(3), .disabled(0), .enable("false")) multiplexer_2 (
    .in0(Flag_q), .in1(register_1_q), .out(multiplexer_2_out), .sel(FlagSelector));

  // Other names for the same wires on the sheet: ALUOP_t[3:0] = ALUOP[3:0]; ADDR[1:0] = ALUOP[5:4];
  //   CarryFlag = FlagRegisterOut[0]; ALU_B[1:0] = RegisterCtrl[1:0]; ALU_A = RegisterCtrl[2];
  //   WRSel[1:0] = RegisterCtrl[4:3]; WriteBackSel[2:0] = RegisterCtrl[7:5]

  // Notes on the sheet:
  //   Writeback
  //   Selector
  //   238
  //   内部レジスタ
  //   出力イネーブル付きバッファ541
  //   2to1 157x2
  //   139でOEコントロール
  //   4to1 153x4
  //   S Z C
  //   74x2 Jccの近く
  //   S Z C
endmodule

module CLK_GEN (
  input  CLK,
  input  Reset,
  output T1,
  output T2,
  output T3,
  output nRST
);

  wire and_1_out, d_ff_1_q, d_ff_2_q, d_ff_6_qn, not_1_out, not_2_out, not_3_out, not_4_out, not_5_out,
       not_6_out, not_7_out, not_8_out, not_9_out, PowerOnReset_q;

  not not_1 (not_1_out, CLK);
  not not_2 (not_2_out, Reset);
  D_Flip_Flop PowerOnReset (.clk(not_1_out), .D(1'b1), .Q(PowerOnReset_q));  // open: Qn, preset, en, reset
  D_Flip_Flop d_ff_1 (.clk(not_1_out), .D(1'b1), .Q(d_ff_1_q), .reset(not_3_out));  // open: Qn, preset, en
  not not_3 (not_3_out, and_1_out);
  and and_1 (and_1_out, not_2_out, PowerOnReset_q);
  D_Flip_Flop d_ff_2 (.clk(not_1_out), .D(d_ff_1_q), .Q(d_ff_2_q), .reset(not_4_out));  // open: Qn, preset, en
  not not_4 (not_4_out, and_1_out);
  not not_5 (not_5_out, not_1_out);
  D_Flip_Flop d_ff_3 (.clk(not_1_out), .D(d_ff_2_q), .Q(nRST), .reset(not_6_out));  // open: Qn, preset, en
  not not_6 (not_6_out, and_1_out);
  D_Flip_Flop d_ff_4 (.clk(not_5_out), .D(d_ff_6_qn), .Q(T1), .reset(not_7_out));  // open: Qn, preset, en
  not not_7 (not_7_out, nRST);
  D_Flip_Flop d_ff_5 (.clk(not_5_out), .D(T1), .Q(T2), .reset(not_8_out));  // open: Qn, preset, en
  not not_8 (not_8_out, nRST);
  D_Flip_Flop d_ff_6 (.clk(not_5_out), .D(T2), .Q(T3), .Qn(d_ff_6_qn), .reset(not_9_out));  // open: preset, en
  not not_9 (not_9_out, nRST);

  // Notes on the sheet:
  //   LogiSimのシミュレーションリセット対応
  //   74x3またはリセット部分を省略して7474x2 175x2でも
endmodule

module SR_Latch (
  input  nS,
  input  nR,
  output nY
);

  wire nand_2_out;

  nand nand_1 (nY, nS, nand_2_out);
  nand nand_2 (nand_2_out, nY, nR);
endmodule

module uROM (
  input  [7:0] OpeCode,
  input  Load,
  input  Update,
  output [11:0] STEP_MON,
  output [15:0] CtrlSignal
);

  wire not_1_out;

  Counter #(.width(4), .max('hf)) _161 (
    .load(Load), .D(4'b0000), .count(not_1_out), .Q(STEP_MON[3:0]), .clk(Update));  // open: carry, clr
  not not_1 (not_1_out, Load);
  Register _377 (.D(OpeCode), .en(Load), .Q(STEP_MON[11:4]), .clk(Update));  // open: clr
  ROM #(.addrWidth(12), .dataWidth(16)) rom_1 (.addr(STEP_MON), .data(CtrlSignal));  // open: sel

  // Notes on the sheet:
  //   contents of rom_1 (hex, n*v repeats v):
  //   c0e0 15*0 4919 d0d9 14*0 4078 10d9 4078 4900 d0d9 11*0 4078 58 4900 d0d9 12*0 4909 d0d9 14*0 4911
  //   d0d9 14*0 4939 a6f 92a e4e 4901 d0d9 10*0 4939 a77 932 e56 4901 d0d9 138*0 4979 10d9 4959 10d9 c080
  //   11*0 4979 10d9 4959 10d9 c0a0 107*0 4939 a6f 92a e4e 4921 5941 865 4901 d0d9 55*0 88e8 c0e8 222*0
  //   94a 96b 90 c0a4 604*0 c90b 143*0 40 60 c080 125*0 4979 10d9 4959 10d9 c0a0 107*0 60 40 c080 13*0 60
  //   40 c0a0 157*0 4979 10d9 4959 10d9 4921 5941 864 a6f 922 c4e c080 197*0 20 ca00 14*0 4038 10d9 ca00
  //   109*0 20 cb00 14*0 4038 10d9 cb00 109*0 20 cc00 14*0 4038 10d9 cc00 109*0 20 cd00 14*0 4038 10d9
  //   cd00 109*0 20 c100 14*0 4038 10d9 c100 109*0 20 cbe0 14*0 4038 10d9 cbe0 109*0 20 c300 14*0 4038
  //   10d9 c300 109*0 20 c200 14*0 4038 10d9 c200 365*0 c500 127*0 c600 127*0 e0 20 644 664 4921 7961 844
  //   c0c0 8*0 40f8 d0d9 206*0 4939 10d9 e0d8 13*0 d0d9 15*0 c000 79*0 24 c524 14*0 f24 424 ca24 29*0 4979
  //   10d9 4959 10d9 30b0 93a 8814 30b0 93b 8814 c0c0 37*0 4971 10b0 4951 10b0 c0c0 43*0 4979 10d9 4959
  //   10d9 c0c0
endmodule

module uROM8 (
  input  [7:0] OpeCode,
  input  Load,
  input  Update,
  input  nQ,
  output [11:0] STEP_MON,
  output [15:0] CtrlSignal
);

  wire not_1_out;

  Counter #(.width(4), .max('hf)) _161 (
    .load(Load), .D(4'b0000), .count(not_1_out), .Q(STEP_MON[3:0]), .clk(Update));  // open: carry, clr
  not not_1 (not_1_out, Load);
  Register _377 (.D(OpeCode), .en(Load), .Q(STEP_MON[11:4]), .clk(Update));  // open: clr
  ROM #(.addrWidth(13)) rom_1 (.addr({STEP_MON, nQ}), .data(CtrlSignal[15:8]));  // open: sel
  Register register_1 (.D(CtrlSignal[15:8]), .Q(CtrlSignal[7:0]), .clk(nQ));  // open: en, clr

  // Notes on the sheet:
  //   contents of rom_1 (hex, n*v repeats v):
  //   e0 c0 30*0 19 49 d9 d0 28*0 78 40 d9 10 78 40 0 49 d9 d0 22*0 78 40 58 0 0 49 d9 d0 24*0 9 49 d9 d0
  //   28*0 11 49 d9 d0 28*0 39 49 6f a 2a 9 4e e 1 49 d9 d0 20*0 39 49 77 a 32 9 56 e 1 49 d9 d0 276*0 79
  //   49 d9 10 59 49 d9 10 80 c0 22*0 79 49 d9 10 59 49 d9 10 a0 c0 214*0 39 49 6f a 2a 9 4e e 21 49 41 59
  //   65 8 1 49 d9 d0 110*0 e8 88 e8 c0 444*0 4a 9 6b 9 90 0 a4 c0 24*0 40 0 79 49 d9 10 21 49 e0 88 0 c9
  //   1172*0 b c9 286*0 40 0 60 0 80 c0 250*0 79 49 d9 10 59 49 d9 10 a0 c0 214*0 60 0 40 0 80 c0 26*0 60
  //   0 40 0 a0 c0 314*0 79 49 d9 10 59 49 d9 10 21 49 41 59 64 8 6f a 22 9 4e c 80 c0 394*0 20 0 0 ca
  //   28*0 38 40 d9 10 0 ca 26*0 78 40 d9 10 58 40 d9 10 39 40 0 ca 180*0 20 0 0 cb 28*0 38 40 d9 10 0 cb
  //   26*0 78 40 d9 10 58 40 d9 10 39 40 0 cb 180*0 20 0 0 cc 28*0 38 40 d9 10 0 cc 26*0 78 40 d9 10 58 40
  //   d9 10 39 40 0 cc 180*0 20 0 0 cd 28*0 38 40 d9 10 0 cd 26*0 78 40 d9 10 58 40 d9 10 39 40 0 cd 180*0
  //   20 0 0 c1 28*0 38 40 d9 10 0 c1 26*0 78 40 d9 10 58 40 d9 10 39 40 0 c1 180*0 20 0 e0 cb 28*0 38 40
  //   d9 10 e0 cb 26*0 78 40 d9 10 58 40 d9 10 39 40 e0 cb 180*0 20 0 0 c3 28*0 38 40 d9 10 0 c3 26*0 78
  //   40 d9 10 58 40 d9 10 39 40 0 c3 180*0 20 0 0 c2 28*0 38 40 d9 10 0 c2 26*0 78 40 d9 10 58 40 d9 10
  //   39 40 0 c2 693*0 c5 255*0 c6 254*0 e0 0 20 0 44 6 64 6 21 49 61 79 44 8 c0 c0 16*0 f8 40 d9 d0 412*0
  //   39 49 d9 10 dc e8 26*0 d9 d0 30*0 e0 c0 158*0 24 0 24 c5 28*0 24 f 24 4 24 ca 58*0 79 49 d9 10 59 49
  //   d9 10 b0 30 3a 9 14 88 b0 30 3b 9 14 88 c0 c0 74*0 71 49 b0 10 51 49 b0 10 c0 c0 55*0 c0 30*0 79 49
  //   59 59 c0 c0 26*0 69 49 49 59 c0 c0
endmodule

module D_FF16 (
  input  [15:0] In,
  input  CLK,
  output [15:0] Out
);

  Register register_1 (.D(In[7:0]), .Q(Out[7:0]), .clk(CLK));  // open: en, clr
  Register register_2 (.D(In[15:8]), .Q(Out[15:8]), .clk(CLK));  // open: en, clr
endmodule

module D_FF8 (
  input  [7:0] In,
  input  CLK,
  input  nOE,
  output [7:0] Out
);

  wire not_1_out;
  wire [7:0] register_1_q;

  not not_1 (not_1_out, nOE);
  Register register_1 (.D(In), .Q(register_1_q), .clk(CLK));  // open: en, clr
  assign Out = not_1_out ? register_1_q : 8'bz;  // Controlled_Buffer controlled_buffer_1
endmodule

module ALU (
  input  [7:0] A,
  input  [7:0] B,
  input  Carry,
  input  [8:0] OpIn,
  output [7:0] LOutMon,
  output ZF,
  output [7:0] ALU_OUT,
  output Carry_2
);

  wire alu8a_1_cy, and_1_out, ext_1_cout, not_1_out, xor_1_out;
  wire [7:0] alu8a_1_y;

  // Probe on OpIn[3:0]
  and and_1 (and_1_out, Carry, OpIn[6]);
  ALU8L alu8l_1 (.A(A), .B(B), .S(OpIn[3:0]), .Y(LOutMon));
  xor xor_1 (xor_1_out, and_1_out, OpIn[5]);
  // Probe on LOutMon
  ALU8A alu8a_1 (.B(LOutMon), .A(A), .Cin(xor_1_out), .CY(alu8a_1_cy), .Y(alu8a_1_y));
  Ext ext_1 (
    .A(LOutMon), .Y(ALU_OUT), .ExOpe(OpIn[8]), .SHR_SXT(OpIn[7]), .COut(ext_1_cout), .CinL(Carry),
    .CinA(alu8a_1_cy), .M(OpIn[4]));
  // Probe on alu8a_1_y
  assign ALU_OUT = not_1_out ? alu8a_1_y : 8'bz;  // Controlled_Buffer controlled_buffer_1
  not not_1 (not_1_out, OpIn[4]);
  ZeroFlag zeroflag_1 (.A(ALU_OUT), .Y(ZF));
  xor xor_2 (Carry_2, ext_1_cout, OpIn[5]);

  // Notes on the sheet:
  //   ExOpe
  //   SHR/SXT
  //   4078
endmodule

module INC_DEC16 (
  input  [1:0] Addr,
  input  [15:0] IN,
  input  [7:0] Offset8,
  output INC,
  output DEC,
  output [15:0] OUT
);

  wire adder4_1_cout, adder4_2_cout, addr_op_1_co, addr_op_1_op, and_1_out, not_1_out, not_2_out;
  wire [7:0] controlled_buffer_1_out;

  // Probe on IN
  // Probe on Offset8
  assign controlled_buffer_1_out = and_1_out ? Offset8 : 8'bz;  // Controlled_Buffer controlled_buffer_1
  assign controlled_buffer_1_out = not_1_out ? {{7{Addr[1]}}, Addr[0]} : 8'bz;  // Controlled_Buffer controlled_buffer_2
  not not_1 (not_1_out, and_1_out);
  and and_1 (and_1_out, ~Addr[0], Addr[1]);  // AND_Gate
  ADDR_OP addr_op_1 (
    .CY(adder4_2_cout), .DEC(Addr[1]), .ADD(Addr[0]), .D7(controlled_buffer_1_out[7]), .CO(addr_op_1_co),
    .OP(addr_op_1_op));
  ADDER4 adder4_1 (.B(controlled_buffer_1_out[3:0]), .A(IN[3:0]), .CIn(1'b0), .COut(adder4_1_cout), .Y(OUT[3:0]));
  ADDER4 adder4_2 (
    .B(controlled_buffer_1_out[7:4]), .A(IN[7:4]), .CIn(adder4_1_cout), .COut(adder4_2_cout), .Y(OUT[7:4]));
  DEC_INC8 dec_inc8_1 (.CI(addr_op_1_co), .A(IN[15:8]), .INC_DEC(addr_op_1_op), .Y(OUT[15:8]));
  not not_2 (not_2_out, Addr[1]);
  // Probe on OUT
  and and_2 (INC, Addr[0], not_2_out);
  and and_3 (DEC, Addr[0], Addr[1]);

  // Notes on the sheet:
  //   CALC/THRU
  //   DEC/INC
  //   GAL16
  //   HC283
  //   GAL22
endmodule

module DEC_INC8 (
  input  CI,
  input  [7:0] A,
  input  INC_DEC,
  output [7:0] Y
);

  wire and_1_out, and_2_out, and_3_out, and_4_out, and_5_out, and_6_out, and_7_out, and_8_out, and_9_out,
       and_10_out, and_11_out, and_12_out, and_13_out, and_14_out, multiplexer_1_out, multiplexer_2_out,
       multiplexer_3_out, multiplexer_4_out, multiplexer_5_out, multiplexer_6_out, multiplexer_7_out;

  and and_1 (and_1_out, CI, A[0]);
  and and_2 (and_2_out, CI, ~A[0]);  // AND_Gate
  and and_3 (and_3_out, and_1_out, A[1]);
  and and_4 (and_4_out, and_2_out, ~A[1]);  // AND_Gate
  and and_5 (and_5_out, and_3_out, A[2]);
  and and_6 (and_6_out, and_4_out, ~A[2]);  // AND_Gate
  and and_7 (and_7_out, and_5_out, A[3]);
  and and_8 (and_8_out, and_6_out, ~A[3]);  // AND_Gate
  and and_9 (and_9_out, and_7_out, A[4]);
  and and_10 (and_10_out, and_8_out, ~A[4]);  // AND_Gate
  and and_11 (and_11_out, and_9_out, A[5]);
  and and_12 (and_12_out, and_10_out, ~A[5]);  // AND_Gate
  and and_13 (and_13_out, and_11_out, A[6]);
  and and_14 (and_14_out, and_12_out, ~A[6]);  // AND_Gate
  xor xor_1 (Y[0], CI, A[0]);
  Multiplexer #(.disabled(0), .enable("false")) multiplexer_1 (
    .in0(and_1_out), .in1(and_2_out), .out(multiplexer_1_out), .sel(INC_DEC));
  xor xor_2 (Y[1], multiplexer_1_out, A[1]);
  Multiplexer #(.disabled(0), .enable("false")) multiplexer_2 (
    .in0(and_3_out), .in1(and_4_out), .out(multiplexer_2_out), .sel(INC_DEC));
  xor xor_3 (Y[2], multiplexer_2_out, A[2]);
  Multiplexer #(.disabled(0), .enable("false")) multiplexer_3 (
    .in0(and_5_out), .in1(and_6_out), .out(multiplexer_3_out), .sel(INC_DEC));
  xor xor_4 (Y[3], multiplexer_3_out, A[3]);
  Multiplexer #(.disabled(0), .enable("false")) multiplexer_4 (
    .in0(and_7_out), .in1(and_8_out), .out(multiplexer_4_out), .sel(INC_DEC));
  xor xor_5 (Y[4], multiplexer_4_out, A[4]);
  Multiplexer #(.disabled(0), .enable("false")) multiplexer_5 (
    .in0(and_9_out), .in1(and_10_out), .out(multiplexer_5_out), .sel(INC_DEC));
  xor xor_6 (Y[5], multiplexer_5_out, A[5]);
  Multiplexer #(.disabled(0), .enable("false")) multiplexer_6 (
    .in0(and_11_out), .in1(and_12_out), .out(multiplexer_6_out), .sel(INC_DEC));
  xor xor_7 (Y[6], multiplexer_6_out, A[6]);
  Multiplexer #(.disabled(0), .enable("false")) multiplexer_7 (
    .in0(and_13_out), .in1(and_14_out), .out(multiplexer_7_out), .sel(INC_DEC));
  xor xor_8 (Y[7], multiplexer_7_out, A[7]);

  // Other names for the same wires on the sheet: DEC = INC_DEC
endmodule

module ADDER4 (
  input  [3:0] A,
  input  [3:0] B,
  input  CIn,
  output COut,
  output [3:0] Y
);

  wire and_1_out, and_2_out, and_3_out, and_4_out, and_5_out, and_6_out, and_7_out, and_8_out, or_1_out,
       or_2_out, or_3_out, or_4_out, or_6_out, or_7_out, or_8_out, xor_1_out, xor_2_out, xor_3_out, xor_4_out;

  xor xor_1 (xor_1_out, B[3], A[3]);
  and and_1 (and_1_out, B[3], A[3]);
  or or_1 (or_1_out, A[3], B[3]);
  and and_2 (and_2_out, or_1_out, or_6_out);
  xor xor_2 (xor_2_out, B[2], A[2]);
  and and_3 (and_3_out, B[2], A[2]);
  or or_2 (or_2_out, A[2], B[2]);
  and and_4 (and_4_out, or_2_out, or_7_out);
  xor xor_3 (xor_3_out, B[1], A[1]);
  and and_5 (and_5_out, B[1], A[1]);
  or or_3 (or_3_out, A[1], B[1]);
  and and_6 (and_6_out, or_3_out, or_8_out);
  xor xor_4 (xor_4_out, B[0], A[0]);
  and and_7 (and_7_out, B[0], A[0]);
  or or_4 (or_4_out, B[0], A[0]);
  and and_8 (and_8_out, or_4_out, CIn);
  or or_5 (COut, and_1_out, and_2_out);
  or or_6 (or_6_out, and_3_out, and_4_out);
  or or_7 (or_7_out, and_5_out, and_6_out);
  or or_8 (or_8_out, and_7_out, and_8_out);
  xor xor_5 (Y[3], xor_1_out, or_6_out);
  xor xor_6 (Y[2], xor_2_out, or_7_out);
  xor xor_7 (Y[1], xor_3_out, or_8_out);
  xor xor_8 (Y[0], xor_4_out, CIn);
endmodule

module ADDR_OP (
  input  CY,
  input  DEC,
  input  ADD,
  input  D7,
  output CO,
  output OP
);

  wire and_1_out, and_2_out, and_3_out, or_1_out, or_2_out;

  and and_1 (and_1_out, ~CY, DEC, or_1_out);  // AND_Gate
  or or_1 (or_1_out, ADD, D7);
  and and_2 (and_2_out, CY, ~DEC);  // AND_Gate
  and and_3 (and_3_out, CY, DEC, ~ADD, ~D7);  // AND_Gate
  or or_2 (or_2_out, D7, ADD);
  or or_3 (CO, and_1_out, and_2_out, and_3_out);
  and and_4 (OP, or_2_out, DEC);
endmodule

module OPGen (
  input  [3:0] OPin,
  output [8:0] OpOut,
  output [3:0] OP,
  output FL
);

  wire optable_1_nfl;

  OpTable optable_1 (
    .A2(OPin[3]), .A1(OPin[2]), .A0(OPin[1]), .D3(OP[3]), .M(OPin[0]), .D2(OP[2]), .D1(OP[1]), .D0(OP[0]),
    .MO(OpOut[4]), .Ci(OpOut[6]), .nFL(optable_1_nfl), .CInv(OpOut[5]));
  and and_1 (OpOut[8], OPin[0], OPin[1], OPin[2]);
  not not_1 (FL, optable_1_nfl);

  assign {OpOut[7], OpOut[3:0]} = {OPin[3], OP};

  // Notes on the sheet:
  //   Jcc Detector で余ってる３AND使いたい
  //   ExOpe
  //   SHR/SXT
endmodule

module OpTable (
  input  A2,
  input  A1,
  input  A0,
  input  M,
  output D3,
  output D2,
  output D1,
  output D0,
  output MO,
  output Ci,
  output nFL,
  output CInv
);

  wire and_1_out, and_2_out, and_3_out, and_4_out, and_5_out, and_6_out, and_7_out, and_8_out, and_9_out,
       and_11_out, and_12_out, and_13_out, and_14_out, and_15_out, and_16_out, and_17_out, and_18_out,
       and_19_out, and_20_out, and_21_out, and_22_out, and_23_out, and_24_out, and_25_out, and_26_out,
       and_27_out, not_1_out, not_2_out, not_3_out, not_4_out, not_5_out, not_6_out, not_7_out, not_8_out,
       not_9_out, not_10_out, not_11_out, not_12_out, not_13_out, not_14_out, not_15_out, not_16_out,
       not_17_out, not_18_out, not_19_out, not_20_out, not_21_out, not_22_out, not_23_out, not_24_out,
       not_25_out, not_26_out, not_27_out, not_28_out, not_29_out, not_30_out, not_31_out, not_32_out,
       not_33_out, not_34_out, not_35_out, not_36_out, not_37_out, not_38_out, not_39_out, not_40_out,
       not_41_out;

  not not_1 (not_1_out, A1);
  and and_1 (and_1_out, not_1_out, not_2_out, M);
  not not_2 (not_2_out, A0);
  not not_3 (not_3_out, A2);
  and and_2 (and_2_out, not_3_out, A0, not_4_out);
  not not_4 (not_4_out, M);
  and and_3 (and_3_out, A1, A0, M);
  and and_4 (and_4_out, A2, not_5_out, not_6_out);
  not not_5 (not_5_out, A1);
  not not_6 (not_6_out, M);
  not not_7 (not_7_out, A0);
  and and_5 (and_5_out, A2, not_7_out, not_8_out);
  not not_8 (not_8_out, M);
  not not_9 (not_9_out, A2);
  not not_10 (not_10_out, A1);
  not not_11 (not_11_out, A1);
  not not_12 (not_12_out, M);
  not not_13 (not_13_out, A2);
  not not_14 (not_14_out, M);
  not not_15 (not_15_out, A0);
  not not_16 (not_16_out, M);
  not not_17 (not_17_out, A1);
  not not_18 (not_18_out, A0);
  not not_19 (not_19_out, A2);
  not not_20 (not_20_out, A1);
  not not_21 (not_21_out, A0);
  not not_22 (not_22_out, M);
  not not_23 (not_23_out, A2);
  not not_24 (not_24_out, M);
  not not_25 (not_25_out, A1);
  not not_26 (not_26_out, A0);
  not not_27 (not_27_out, A2);
  and and_6 (and_6_out, not_27_out, not_28_out);
  not not_28 (not_28_out, A1);
  not not_29 (not_29_out, A2);
  not not_30 (not_30_out, A0);
  and and_7 (and_7_out, not_29_out, not_30_out, not_31_out);
  not not_31 (not_31_out, M);
  not not_32 (not_32_out, A1);
  and and_8 (and_8_out, not_32_out, not_33_out);
  not not_33 (not_33_out, A0);
  and and_9 (and_9_out, A1, A0, M);
  and and_10 (Ci, A2, A1);
  not not_34 (not_34_out, A1);
  not not_35 (not_35_out, A0);
  not not_36 (not_36_out, M);
  not not_37 (not_37_out, A2);
  not not_38 (not_38_out, A1);
  not not_39 (not_39_out, A0);
  not not_40 (not_40_out, A0);
  not not_41 (not_41_out, A1);
  or or_1 (D3, and_1_out, and_2_out, and_3_out, and_4_out, and_5_out);
  and and_11 (and_11_out, not_9_out, not_10_out, A0);
  and and_12 (and_12_out, not_11_out, A0, not_12_out);
  and and_13 (and_13_out, not_13_out, A1, not_14_out);
  and and_14 (and_14_out, A1, not_15_out, not_16_out);
  and and_15 (and_15_out, A2, not_17_out, not_18_out, M);
  and and_16 (and_16_out, not_19_out, A0);
  and and_17 (and_17_out, A0, M);
  and and_18 (and_18_out, A2, not_20_out, not_21_out, not_22_out);
  and and_19 (and_19_out, A2, A1, M);
  and and_20 (and_20_out, not_23_out, A1, not_24_out);
  or or_2 (D0, and_20_out, and_21_out, and_22_out);
  and and_21 (and_21_out, A2, not_25_out, A0, M);
  and and_22 (and_22_out, A2, A1, not_26_out, M);
  or or_3 (MO, and_6_out, and_7_out, and_8_out, and_9_out);
  and and_23 (and_23_out, not_34_out, not_35_out, not_36_out);
  and and_24 (and_24_out, not_37_out, A1, A0, M);
  or or_4 (nFL, and_23_out, and_24_out, and_25_out);
  and and_25 (and_25_out, A2, not_38_out, not_39_out);
  and and_26 (and_26_out, A1, not_40_out, M);
  or or_5 (CInv, and_26_out, and_27_out);
  and and_27 (and_27_out, A2, not_41_out, A0, M);
  or or_6 (D2, and_11_out, and_12_out, and_13_out, and_14_out, and_15_out);
  or or_7 (D1, and_16_out, and_17_out, and_18_out, and_19_out);
endmodule

module Ext (
  input  [7:0] A,
  input  CinL,
  input  CinA,
  input  ExOpe,
  input  SHR_SXT,
  input  M,
  output [7:0] Y,
  output COut
);

  wire and_1_out, and_2_out;
  wire [7:0] multiplexer_1_out;

  Multiplexer #(.select(2), .width(8), .disabled(0), .enable("false")) multiplexer_1 (
    .in0(A), .in1(A), .in2({8{A[7]}}), .in3({CinL, A[7:1]}), .out(multiplexer_1_out), .sel({ExOpe, SHR_SXT}));
  assign Y = M ? multiplexer_1_out : 8'bz;  // Controlled_Buffer controlled_buffer_1
  and and_1 (and_1_out, ExOpe, SHR_SXT, A[0]);
  or or_1 (COut, and_1_out, and_2_out);
  and and_2 (and_2_out, CinA, ~M);  // AND_Gate

  // Notes on the sheet:
  //   SHR/SXTはALUOPのbit0
  //   GAL22
endmodule

module ALU8L (
  input  [7:0] A,
  input  [7:0] B,
  input  [3:0] S,
  output [7:0] Y
);

  // Probe on S
  Multiplexer #(.select(2), .disabled(0), .enable("false")) multiplexer_1 (
    .in0(S[0]), .in1(S[1]), .in2(S[2]), .in3(S[3]), .out(Y[4]), .sel({B[4], A[4]}));
  Multiplexer #(.select(2), .disabled(0), .enable("false")) multiplexer_2 (
    .in0(S[0]), .in1(S[1]), .in2(S[2]), .in3(S[3]), .out(Y[5]), .sel({B[5], A[5]}));
  Multiplexer #(.select(2), .disabled(0), .enable("false")) multiplexer_3 (
    .in0(S[0]), .in1(S[1]), .in2(S[2]), .in3(S[3]), .out(Y[6]), .sel({B[6], A[6]}));
  Multiplexer #(.select(2), .disabled(0), .enable("false")) multiplexer_4 (
    .in0(S[0]), .in1(S[1]), .in2(S[2]), .in3(S[3]), .out(Y[7]), .sel({B[7], A[7]}));
  Multiplexer #(.select(2), .disabled(0), .enable("false")) multiplexer_5 (
    .in0(S[0]), .in1(S[1]), .in2(S[2]), .in3(S[3]), .out(Y[0]), .sel({B[0], A[0]}));
  Multiplexer #(.select(2), .disabled(0), .enable("false")) multiplexer_6 (
    .in0(S[0]), .in1(S[1]), .in2(S[2]), .in3(S[3]), .out(Y[1]), .sel({B[1], A[1]}));
  Multiplexer #(.select(2), .disabled(0), .enable("false")) multiplexer_7 (
    .in0(S[0]), .in1(S[1]), .in2(S[2]), .in3(S[3]), .out(Y[2]), .sel({B[2], A[2]}));
  Multiplexer #(.select(2), .disabled(0), .enable("false")) multiplexer_8 (
    .in0(S[0]), .in1(S[1]), .in2(S[2]), .in3(S[3]), .out(Y[3]), .sel({B[3], A[3]}));

  // Notes on the sheet:
  //   F16
  //   F16
endmodule

module ALU4A (
  input  [3:0] B,
  input  [3:0] A,
  input  CIn,
  output COut,
  output [3:0] Y
);

  wire and_1_out, and_2_out, and_3_out, and_4_out, and_5_out, and_6_out, and_7_out, and_8_out, and_9_out,
       and_10_out, and_11_out, and_12_out, and_13_out, and_14_out, or_1_out, or_2_out, or_3_out, xor_1_out,
       xor_2_out, xor_3_out, xor_4_out;

  xor xor_1 (xor_1_out, B[3], A[3]);
  and and_1 (and_1_out, B[3], A[3]);
  xor xor_2 (xor_2_out, B[2], A[2]);
  and and_2 (and_2_out, B[2], A[2]);
  xor xor_3 (xor_3_out, B[1], A[1]);
  and and_3 (and_3_out, B[1], A[1]);
  xor xor_4 (xor_4_out, B[0], A[0]);
  and and_4 (and_4_out, B[0], A[0]);
  and and_5 (and_5_out, xor_1_out, and_2_out);
  and and_6 (and_6_out, xor_1_out, xor_2_out, and_3_out);
  and and_7 (and_7_out, xor_1_out, xor_2_out, xor_3_out, and_4_out);
  and and_8 (and_8_out, xor_1_out, xor_2_out, xor_3_out, xor_4_out, CIn);
  and and_9 (and_9_out, xor_2_out, and_3_out);
  and and_10 (and_10_out, xor_2_out, xor_3_out, and_4_out);
  and and_11 (and_11_out, xor_2_out, xor_3_out, xor_4_out, CIn);
  and and_12 (and_12_out, xor_3_out, and_4_out);
  and and_13 (and_13_out, xor_3_out, xor_4_out, CIn);
  and and_14 (and_14_out, xor_4_out, CIn);
  or or_1 (or_1_out, and_2_out, and_9_out, and_10_out, and_11_out);
  or or_2 (or_2_out, and_3_out, and_12_out, and_13_out);
  or or_3 (or_3_out, and_4_out, and_14_out);
  or or_4 (COut, and_1_out, and_5_out, and_6_out, and_7_out, and_8_out);
  xor xor_5 (Y[3], xor_1_out, or_1_out);
  xor xor_6 (Y[2], xor_2_out, or_2_out);
  xor xor_7 (Y[1], xor_3_out, or_3_out);
  xor xor_8 (Y[0], xor_4_out, CIn);
endmodule

module ALU8A (
  input  [7:0] B,
  input  [7:0] A,
  input  Cin,
  output CY,
  output [7:0] Y
);

  wire alu4a_2_cout;

  ALU4A alu4a_1 (.B(B[7:4]), .A(A[7:4]), .CIn(alu4a_2_cout), .COut(CY), .Y(Y[7:4]));
  ALU4A alu4a_2 (.B(B[3:0]), .A(A[3:0]), .CIn(Cin), .COut(alu4a_2_cout), .Y(Y[3:0]));
endmodule

module ZeroFlag (
  input  [7:0] A,
  output Y
);

  nor nor_1 (Y, A[0], A[1], A[2], A[3], A[4], A[5], A[6], A[7]);
endmodule

module MUX4to1x8 (
  input  [7:0] D0,
  input  [7:0] D1,
  input  [7:0] D2,
  input  [7:0] D3,
  input  [1:0] Sel,
  output [7:0] Y,
  output I0,
  output I1,
  output I2,
  output I3
);

  Multiplexer #(.select(2), .width(8), .enable("false")) multiplexer_1 (
    .in0(D0), .in1(D1), .in2(D2), .in3(D3), .out(Y), .sel(Sel));
  Demultiplexer #(.select(2), .disabled(0), .enable("false")) demultiplexer_1 (
    .out0(I0), .out1(I1), .out2(I2), .out3(I3), .in(1'b1), .sel(Sel));

  // Notes on the sheet:
  //   139
endmodule

module MUX4to1x16 (
  input  [15:0] D0,
  input  [15:0] D1,
  input  [15:0] D2,
  input  [15:0] D3,
  input  [1:0] Sel,
  output [15:0] Y,
  output I0,
  output I1,
  output I2,
  output I3
);

  Multiplexer #(.select(2), .width(16), .disabled(0), .enable("false")) multiplexer_1 (
    .in0(D0), .in1(D1), .in2(D2), .in3(D3), .out(Y), .sel(Sel));
  Demultiplexer #(.select(2), .disabled(0), .enable("false")) demultiplexer_1 (
    .out0(I0), .out1(I1), .out2(I2), .out3(I3), .in(1'b1), .sel(Sel));

  // Notes on the sheet:
  //   139
endmodule

module OP (
  input  S1,
  input  S0,
  input  D0,
  input  D1,
  input  D2,
  input  D3,
  input  D4,
  input  D5,
  input  D6,
  input  D7,
  output Q0,
  output Q1,
  output Q2,
  output Q3,
  output Q4,
  output Q5,
  output Q6,
  output Q7
);

  wire and_1_out, not_1_out;

  assign {Q7, Q6, Q5, Q4, Q3, Q2, Q1, Q0} = not_1_out ? {{7{S0}}, S1} : 8'bz;  // Controlled_Buffer controlled_buffer_1
  not not_1 (not_1_out, and_1_out);
  assign {Q7, Q6, Q5, Q4, Q3, Q2, Q1, Q0} = and_1_out ? {D7, D6, D5, D4, D3, D2, D1, D0} : 8'bz;  // Controlled_Buffer controlled_buffer_2
  and and_1 (and_1_out, ~S1, S0);  // AND_Gate
endmodule

module OP_T (
  input  S1,
  input  S0,
  input  D0,
  input  D1,
  input  D2,
  input  D3,
  input  D4,
  input  D5,
  input  D6,
  input  D7,
  output Q0,
  output Q1,
  output Q2,
  output Q3,
  output Q4,
  output Q5,
  output Q6,
  output Q7
);

  wire and_1_out, and_2_out, and_3_out, and_4_out, and_5_out, and_6_out, and_7_out, and_8_out, and_9_out,
       and_10_out, and_11_out, and_12_out, and_13_out, and_14_out, and_15_out;

  and and_1 (and_1_out, S0, D0);
  and and_2 (and_2_out, S0, D1);
  and and_3 (and_3_out, S1, S0);
  and and_4 (and_4_out, S0, D2);
  and and_5 (and_5_out, S1, S0);
  and and_6 (and_6_out, S0, D3);
  and and_7 (and_7_out, S1, S0);
  and and_8 (and_8_out, S0, D4);
  and and_9 (and_9_out, S1, S0);
  and and_10 (and_10_out, S0, D5);
  and and_11 (and_11_out, S1, S0);
  and and_12 (and_12_out, S0, D6);
  and and_13 (and_13_out, S1, S0);
  and and_14 (and_14_out, S0, D7);
  and and_15 (and_15_out, S1, S0);
  or or_1 (Q0, and_1_out, S1);
  or or_2 (Q1, and_2_out, and_3_out);
  or or_3 (Q2, and_4_out, and_5_out);
  or or_4 (Q3, and_6_out, and_7_out);
  or or_5 (Q4, and_8_out, and_9_out);
  or or_6 (Q5, and_10_out, and_11_out);
  or or_7 (Q6, and_12_out, and_13_out);
  or or_8 (Q7, and_14_out, and_15_out);
endmodule
