// Logisim project CPU298_B3.circ as structural Verilog: 22 circuits, main circuit PC-298
module PC_298 (
);

  wire Reset_out;
  wire [7:0] keyboard_1_data;
  wire [11:0] system_1_console_out;

  Button Reset (.out(Reset_out));
  System system_1 (.ResetIn(Reset_out), .Console_OUT(system_1_console_out), .Console_IN(keyboard_1_data));
  TTY #(.rows(25), .cols(80)) tty_1 (
    .data(system_1_console_out[6:0]), .clk(system_1_console_out[7]), .we(system_1_console_out[8]),
    .clr(system_1_console_out[9]));
  Keyboard keyboard_1 (
    .clk(system_1_console_out[7]), .re(system_1_console_out[10]), .clr(system_1_console_out[11]),
    .avail(keyboard_1_data[7]), .data(keyboard_1_data[6:0]));

  // Notes on the sheet:
  //   Key Input
endmodule

module System (
  input  ResetIn,
  input  [7:0] Console_IN,
  output [11:0] Console_OUT
);

  wire Clock_out, decoder_1_out0, decoder_1_out1, decoder_1_out2, decoder_1_out3, equal14_1_y,
       n298_core_1_read, n298_core_1_write, not_1_out, not_2_out, or_1_out, or_2_out;
  wire [7:0] n298_core_1_dataout, register_1_q;
  wire [15:0] n298_core_1_addressout;

  Clock Clock (.out(Clock_out));
  _298_CORE u_298_core_1 (
    .Reset(ResetIn), .DataOut(n298_core_1_dataout), .DataIn(n298_core_1_dataout), .Read(n298_core_1_read),
    .AddressOut(n298_core_1_addressout), .Write(n298_core_1_write), .CLK(Clock_out));  // open: S0, S1
  // Probe on n298_core_1_dataout
  // Probe on n298_core_1_addressout
  or or_1 (or_1_out, n298_core_1_read, n298_core_1_write);
  Pull_Resistor pull_resistor_1 (.node(n298_core_1_dataout));
  Pull_Resistor pull_resistor_2 (.node(n298_core_1_addressout));
  // AND_Gate and_1 has open pins: in0=or_1_out, in1=not_1_out, out=open
  Equal14 equal14_1 (.In0(n298_core_1_addressout[15:2]), .In1(14'h3fe0), .Y(equal14_1_y));
  Decoder #(.select(2), .disabled(0)) decoder_1 (
    .out0(decoder_1_out0), .out1(decoder_1_out1), .out2(decoder_1_out2), .out3(decoder_1_out3),
    .sel(n298_core_1_addressout[15:14]));  // open: en
  not not_1 (not_1_out, equal14_1_y);
  and and_2 (Console_OUT[8], equal14_1_y, n298_core_1_write);
  and and_3 (Console_OUT[10], equal14_1_y, n298_core_1_read);
  assign n298_core_1_dataout = Console_OUT[10] ? register_1_q : 8'bz;  // Controlled_Buffer controlled_buffer_1
  RAM #(.addrWidth(14)) ram_1 (
    .addr(n298_core_1_addressout[13:0]), .data(n298_core_1_dataout), .sel(decoder_1_out0),
    .clk(n298_core_1_write), .ld(n298_core_1_read), .clr(1'b0));
  assign Console_OUT[6:0] = Console_OUT[8] ? n298_core_1_dataout[6:0] : 7'bz;  // Controlled_Buffer controlled_buffer_2
  not not_2 (not_2_out, or_2_out);
  not not_3 (Console_OUT[7], not_2_out);
  or or_2 (or_2_out, Console_OUT[8], Console_OUT[10]);
  RAM #(.addrWidth(14)) ram_2 (
    .addr(n298_core_1_addressout[13:0]), .data(n298_core_1_dataout), .sel(decoder_1_out1),
    .clk(n298_core_1_write), .ld(n298_core_1_read), .clr(1'b0));
  Register register_1 (.D(Console_IN), .en(Console_OUT[10]), .Q(register_1_q), .clk(Console_OUT[10]), .clr(ResetIn));
  RAM #(.addrWidth(14)) ram_3 (
    .addr(n298_core_1_addressout[13:0]), .data(n298_core_1_dataout), .sel(decoder_1_out2),
    .clk(n298_core_1_write), .ld(n298_core_1_read), .clr(1'b0));
  ROM #(.addrWidth(14)) rom_1 (.addr(n298_core_1_addressout[13:0]), .data(n298_core_1_dataout), .sel(decoder_1_out3));

  assign {Console_OUT[11], Console_OUT[9]} = {2{ResetIn}};

  // Other names for the same wires on the sheet: Reset = ResetIn

  // Notes on the sheet:
  //   ADDR Decoder
  //   RAM0 0000-3FFF
  //   RAM1 4000-7FFF
  //   RAM2 8000-BFFF
  //   ROM0 C000-FFFF
  //   contents of rom_1 (hex, n*v repeats v):
  //   68 29 0 2 f8 9 c0 ee fb fb c0 ee fb fb 2 0 ee fe 7c 0 f 0 a5 8 e5 fb d6 9 fe e9 ff 48 65 6c 6c 6f 0
  //   6e 48 65 6c 6c 6f 21*0 8 5a 28 0 80 17*0 76 553*0 34 413*0 fe 231*0 76 2553*0 f8 aa 8478*0 6e 4062*0
  //   c0
endmodule

module _298_CORE (
  input  [7:0] DataIn,
  input  CLK,
  input  Reset,
  output [7:0] DataOut,
  output [15:0] AddressOut,
  output Write,
  output S0,
  output Read,
  output S1
);

  wire and_1_out, and_2_out, and_3_out, and_4_out, and_5_out, CLK_t, comparator_1_eq, d_ff_1_q, E, HQ,
       ManualCLK, nand_1_out, nand_2_out, not_1_out, not_2_out, nRST, or_1_out, Q, Resume,
       sequencer_1_jcc_op, sequencer_1_loadopecode, sequencer_1_ndo_jump, sequencer_1_stageclock,
       sequencer_1_stepupdate, \sequencer_1_μrom_address_clk ;
  wire [1:0] sequencer_1_exbuscontrol;
  wire [2:0] executer_1_flagregisterout;
  wire [5:0] sequencer_1_aluop;
  wire [7:0] buffer_1_out, executer_1_dataout, sequencer_1_dataout, sequencer_1_executercontrol,
       sequencer_1_op;
  wire [11:0] sequencer_1_step_monitor;
  wire [15:0] executer_1_addrout;

  // Probe on sequencer_1_op
  Comparator comparator_1 (.a(sequencer_1_op), .b(8'hf0), .eq(comparator_1_eq));  // open: gt, lt
  and and_1 (and_1_out, ~HQ, E);  // AND_Gate
  Executer executer_1 (
    .DataOut(executer_1_dataout), .FlagRegisterOut(executer_1_flagregisterout), .E(E),
    .AddrOut(executer_1_addrout), .DataIn(sequencer_1_dataout), .RegisterCtrl(sequencer_1_executercontrol),
    .STEP(sequencer_1_step_monitor), .ALUOP(sequencer_1_aluop), .Q(Q), .CLK(ManualCLK), .Resume(Resume),
    .HQ(HQ), .in_1(CLK_t));
  // Probe on sequencer_1_executercontrol
  // Probe on sequencer_1_aluop
  Sequencer sequencer_1 (
    .FlagIn(executer_1_flagregisterout), .nReset(nRST), .DataIn(buffer_1_out),
    .ExecuterControl(sequencer_1_executercontrol), .ExBusControl(sequencer_1_exbuscontrol),
    .STEP_Monitor(sequencer_1_step_monitor), .DataOut(sequencer_1_dataout), .Stage_1(S1), .Stage_0(S0),
    .StepUpdate(sequencer_1_stepupdate), .Jcc_OP(sequencer_1_jcc_op), .nDO_JUMP(sequencer_1_ndo_jump),
    .StageClock(sequencer_1_stageclock), .LoadOpeCode(sequencer_1_loadopecode),
    .\μROM_Address_CLK (\sequencer_1_μrom_address_clk ), .ALUOP(sequencer_1_aluop), .Q(Q), .HQ(HQ), .E(E),
    .CLK(CLK_t), .OP(sequencer_1_op));
  D_Flip_Flop d_ff_1 (.clk(not_1_out), .D(1'b0), .Q(d_ff_1_q), .preset(and_2_out));  // open: Qn, en, reset
  not not_1 (not_1_out, Resume);
  and and_2 (and_2_out, comparator_1_eq, and_1_out);
  // Probe on executer_1_dataout
  // Probe on executer_1_addrout
  D_FF8 d_ff8_1 (.In(executer_1_dataout), .CLK(Q), .OE(and_3_out), .Out(DataOut));
  D_FF16 d_ff16_1 (.In(executer_1_addrout), .Out(AddressOut), .CLK(Q));
  Multiplexer #(.disabled(0), .enable("false")) multiplexer_1 (.in0(CLK), .in1(not_2_out), .out(CLK_t), .sel(d_ff_1_q));
  not not_2 (not_2_out, ManualCLK);
  and and_3 (and_3_out, or_1_out, and_4_out);
  or or_1 (or_1_out, Q, HQ);
  and and_4 (and_4_out, ~sequencer_1_exbuscontrol[0], sequencer_1_exbuscontrol[1]);  // AND_Gate
  and and_5 (and_5_out, sequencer_1_exbuscontrol[0], ~sequencer_1_exbuscontrol[1]);  // AND_Gate
  assign buffer_1_out = DataIn;  // Buffer buffer_1, 8 bits wide
  // Probe on DataOut
  // Probe on AddressOut
  nand nand_1 (nand_1_out, and_4_out, HQ);
  not not_3 (Write, nand_1_out);
  nand nand_2 (nand_2_out, and_5_out, HQ);
  not not_4 (Read, nand_2_out);
  // Probe on DataIn
  CLK_GEN clk_gen_1 (.CLK(CLK_t), .Reset(Reset), .nRST(nRST), .T1(Q), .T2(HQ), .T3(E));

  // Notes on the sheet:
  //   Reset: pull=up
  //   574
  //   OE付き D-FF 
  //   Q↑でラッチQ|HQの間出力イネーブル
  //   DataBus_Out
  //   AddressBus
  //   DataBus_In
  //   HCT541
  //   こっちはD-FFを外した
endmodule

module Sequencer (
  input  [7:0] DataIn,
  input  CLK,
  input  nReset,
  input  Q,
  input  HQ,
  input  E,
  input  [2:0] FlagIn,
  output [7:0] OP,
  output [11:0] STEP_Monitor,
  output [7:0] ExecuterControl,
  output LoadOpeCode,
  output [5:0] ALUOP,
  output [1:0] ExBusControl,
  output [7:0] DataOut,
  output StepUpdate,
  output \μROM_Address_CLK ,
  output StageClock,
  output Stage_1,
  output Jcc_OP,
  output Stage_0,
  output nDO_JUMP
);

  wire and_1_out, and_2_out, and_4_out, multiplexer_2_out, nE, nor_1_out, not_4_out, not_5_out, not_6_out,
       not_7_out, not_8_out, not_9_out, nQ, Stage_Bit0_qn, Stage_Bit1_qn;
  wire [3:0] _161_q, JUMP_OP;
  wire [7:0] _377_q, IR_q, OpCode;
  wire [15:0] rom_1_data, urom_1_ctrlsignal;

  not not_1 (nQ, Q);
  not not_2 (\μROM_Address_CLK , HQ);
  not not_3 (nE, E);
  // Probe on {DataIn[7:4], JUMP_OP}
  Register IR (.D({DataIn[7:4], JUMP_OP}), .en(and_1_out), .Q(IR_q), .clk(E));  // open: clr
  and and_1 (and_1_out, Stage_0, Stage_Bit1_qn);
  and and_2 (and_2_out, Stage_1, Stage_Bit0_qn);
  D_Flip_Flop Stage_Bit1 (
    .clk(StageClock), .D(and_1_out), .Q(Stage_1), .Qn(Stage_Bit1_qn), .reset(not_4_out));  // open: preset, en
  D_Flip_Flop Stage_Bit0 (
    .clk(StageClock), .D(Stage_Bit0_qn), .Q(Stage_0), .Qn(Stage_Bit0_qn), .reset(not_4_out));  // open: preset, en
  not not_4 (not_4_out, nReset);
  Multiplexer #(.width(8), .disabled(0), .enable("false")) multiplexer_1 (
    .in0({7'b1110000, Stage_0}), .in1(IR_q), .out(OpCode), .sel(and_2_out));
  not not_5 (not_5_out, StepUpdate);
  // Probe on OpCode
  D_Flip_Flop StepControl (.clk(nQ), .D(not_5_out), .Qn(LoadOpeCode), .reset(not_6_out));  // open: Q, preset, en
  not not_6 (not_6_out, nReset);
  D_Flip_Flop Stage_Control (.clk(nE), .D(StepUpdate), .Qn(StageClock), .reset(not_7_out));  // open: Q, preset, en
  not not_7 (not_7_out, \μROM_Address_CLK );
  // Probe on OpCode
  uROM urom_1 (
    .OpeCode(OpCode), .Load(LoadOpeCode), .Update(\μROM_Address_CLK ), .STEP_MON({OP, STEP_Monitor[3:0]}),
    .CtrlSignal(urom_1_ctrlsignal));
  and and_3 (StepUpdate, urom_1_ctrlsignal[14], urom_1_ctrlsignal[15]);
  not not_8 (not_8_out, LoadOpeCode);
  // Probe on {OP, STEP_Monitor[3:0]}
  // Probe on urom_1_ctrlsignal
  nor nor_1 (nor_1_out, FlagIn[0], FlagIn[1]);
  Counter #(.width(4), .max('hf)) _161 (
    .load(LoadOpeCode), .D(4'b0000), .count(not_8_out), .Q(_161_q), .clk(\μROM_Address_CLK ));  // open: carry, clr
  Register _377 (.D(OpCode), .en(LoadOpeCode), .Q(_377_q), .clk(\μROM_Address_CLK ));  // open: clr
  not not_9 (not_9_out, nReset);
  and and_4 (and_4_out, ~DataIn[4], DataIn[5], DataIn[7]);  // AND_Gate
  Multiplexer #(.select(2), .disabled(0), .enable("false")) multiplexer_2 (
    .in0(FlagIn[0]), .in1(FlagIn[1]), .in2(nor_1_out), .in3(FlagIn[2]), .out(multiplexer_2_out),
    .sel(DataIn[2:1]));
  Register #(.width(16)) Ctrl_signal_register (
    .D(urom_1_ctrlsignal), .Q({ExBusControl, ALUOP, ExecuterControl}), .clk(nE), .clr(not_9_out));  // open: en
  and and_5 (Jcc_OP, ~DataIn[3], and_4_out);  // AND_Gate
  xor xor_1 (nDO_JUMP, DataIn[0], multiplexer_2_out);
  Multiplexer #(.width(4), .disabled(0), .enable("false")) multiplexer_3 (
    .in0(DataIn[3:0]), .in1({3'b111, nDO_JUMP}), .out(JUMP_OP), .sel(Jcc_OP));
  ROM #(.addrWidth(12), .dataWidth(16)) rom_1 (.addr({_377_q, _161_q}), .data(rom_1_data));  // open: sel
  // Probe on rom_1_data

  assign DataOut = DataIn;
  assign STEP_Monitor[11:4] = OP;

  // Other names for the same wires on the sheet: CY = FlagIn[0]; ZF = FlagIn[1]; SF = FlagIn[2]; Load = LoadOpeCode;
  //   StageUpdate = StepUpdate; nHQ = \μROM_Address_CLK ; Update = \μROM_Address_CLK 

  // Notes on the sheet:
  //   nReset: pull=up
  //   Fetch Opecode
  //   377 clken
  //   OP Selector
  //   実行ステージ以外のときは0xEXにする
  //   μROM_IDX
  //   通常HQ↓で変化する
  //   HCT273 AsyncReset
  //   Jcc Detector
  //   contents of rom_1 (hex, n*v repeats v):
  //   c001 31*0 8808 c008 94*0 4939 d0f9 94*0 4959 a8f 94a e6e 4921 d0f9 250*0 4959 a8f 94a e6e 4941 5961
  //   885 4921 d0f9 151*0 4999 10f9 4979 10f9 c0a0 635*0 c92b 271*0 4999 10f9 4979 10f9 c0c0 107*0 80 60
  //   c0a0 13*0 80 60 c0c0 157*0 4999 10f9 4979 10f9 4941 5961 884 a8f 942 c6e c0a0 197*0 840 ca20 1278*0
  //   c520 256*0 40 664 684 4941 7981 864 c0e0 8*0 4018 d0f9 206*0 4959 10f9 a9f 744 c7e c0e0 10*0 d0f9
  //   15*0 c000 127*0 4999 10f9 4979 10f9 30d0 95a 8814 30d0 95b 8814 c0e0 37*0 4991 10d0 4971 10d0 c0e0
  //   43*0 4999 10f9 4979 10f9 c0e0
  //   リセット時の初期化
endmodule

module Executer (
  input  in_1,
  input  Q,
  input  HQ,
  input  E,
  input  [7:0] DataIn,
  input  [11:0] STEP,
  input  [5:0] ALUOP,
  input  [7:0] RegisterCtrl,
  output [2:0] FlagRegisterOut,
  output CLK,
  output Resume,
  output [7:0] DataOut,
  output [15:0] AddrOut
);

  wire and_1_out, decoder_1_out0, decoder_1_out1, decoder_1_out2, decoder_1_out3, decoder_1_out4,
       decoder_1_out5, decoder_1_out6, decoder_1_out7, inc_dec16_1_dec, inc_dec16_1_inc, mux4to1x8_1_i0,
       mux4to1x8_1_i1, mux4to1x8_1_i2, mux4to1x8_1_i3, mux4to1x16_1_i0, mux4to1x16_1_i1, mux4to1x16_1_i2,
       mux4to1x16_1_i3, not_1_out, not_2_out, not_3_out, op_1_fl, op_1_sar;
  wire [1:0] alu_1_carry_2;
  wire [3:0] op_1_op;
  wire [7:0] Acc_q, alu_1_loutmon, controlled_buffer_1_out, H_q, L_q, mux4to1x8_1_y, op_1_opout, W_q;
  wire [15:0] mux4to1x16_1_y, PC_q, X_q, Y_q;

  // Probe on STEP
  not not_1 (not_1_out, Q);
  and and_1 (and_1_out, not_1_out, HQ);
  // Probe on DataIn
  // Probe on RegisterCtrl[7:5]
  Decoder #(.select(3), .disabled(0)) decoder_1 (
    .out0(decoder_1_out0), .out1(decoder_1_out1), .out2(decoder_1_out2), .out3(decoder_1_out3),
    .out4(decoder_1_out4), .out5(decoder_1_out5), .out6(decoder_1_out6), .out7(decoder_1_out7),
    .sel(RegisterCtrl[7:5]), .en(and_1_out));
  Register Acc (.D(DataOut), .Q(Acc_q), .clk(decoder_1_out1));  // open: en, clr
  Register W (.D(DataOut), .Q(W_q), .clk(decoder_1_out2));  // open: en, clr
  Register H (.D(DataOut), .Q(H_q), .clk(decoder_1_out3));  // open: en, clr
  Register L (.D(DataOut), .Q(L_q), .clk(decoder_1_out4));  // open: en, clr
  Register #(.width(16)) X (.D(AddrOut), .Q(X_q), .clk(decoder_1_out5));  // open: en, clr
  Register #(.width(16)) Y (.D(AddrOut), .Q(Y_q), .clk(decoder_1_out6));  // open: en, clr
  Register #(.width(16)) PC (.D(AddrOut), .Q(PC_q), .clk(decoder_1_out7));  // open: en, clr
  // Probe on AddrOut
  assign controlled_buffer_1_out = not_2_out ? Acc_q : 8'bz;  // Controlled_Buffer controlled_buffer_1
  assign controlled_buffer_1_out = RegisterCtrl[2] ? W_q : 8'bz;  // Controlled_Buffer controlled_buffer_2
  not not_2 (not_2_out, RegisterCtrl[2]);
  MUX4to1x8 mux4to1x8_1 (
    .D0(W_q), .D1(DataIn), .D2(AddrOut[15:8]), .D3(AddrOut[7:0]), .Sel(RegisterCtrl[1:0]), .Y(mux4to1x8_1_y),
    .I0(mux4to1x8_1_i0), .I1(mux4to1x8_1_i1), .I2(mux4to1x8_1_i2), .I3(mux4to1x8_1_i3));
  // Probe on DataOut
  MUX4to1x16 mux4to1x16_1 (
    .D0({H_q, L_q}), .D1(X_q), .D2(Y_q), .D3(PC_q), .Sel(RegisterCtrl[4:3]), .Y(mux4to1x16_1_y),
    .I0(mux4to1x16_1_i0), .I1(mux4to1x16_1_i1), .I2(mux4to1x16_1_i2), .I3(mux4to1x16_1_i3));
  // Probe on ALUOP[5:4]
  // Probe on ALUOP[3:0]
  // Probe on op_1_op
  // Probe on controlled_buffer_1_out
  // Probe on mux4to1x8_1_y
  // Probe on mux4to1x16_1_y
  // Probe on alu_1_loutmon
  OP op_1 (.OPin(ALUOP[3:0]), .OP(op_1_op), .OpOut(op_1_opout), .FL(op_1_fl), .SAR(op_1_sar));
  INC_DEC16 inc_dec16_1 (
    .IN(mux4to1x16_1_y), .OUT(AddrOut), .INC_DEC(ALUOP[5]), .CarryIn(ALUOP[4]), .INC(inc_dec16_1_inc),
    .DEC(inc_dec16_1_dec));
  // Probe on {DataOut[7], alu_1_carry_2}
  not not_3 (not_3_out, op_1_fl);
  ALU alu_1 (
    .A(controlled_buffer_1_out), .Carry_2(alu_1_carry_2[0]), .ALU_OUT(DataOut), .ZF(alu_1_carry_2[1]),
    .B(mux4to1x8_1_y), .LOutMon(alu_1_loutmon), .OpIn(op_1_opout), .Carry(FlagRegisterOut[0]), .SAR(op_1_sar));
  Register #(.width(3)) Flag (
    .D({DataOut[7], alu_1_carry_2}), .en(not_3_out), .Q(FlagRegisterOut), .clk(E));  // open: clr
  Button ManualClock (.out(CLK));
  Button u_Resume (.out(Resume));

  // Other names for the same wires on the sheet: ALUOP_t[3:0] = ALUOP[3:0]; ADDR[1:0] = ALUOP[5:4];
  //   CarryFlag = FlagRegisterOut[0]; ZeroFlag = FlagRegisterOut[1]; SignFlag = FlagRegisterOut[2];
  //   ALU_B[1:0] = RegisterCtrl[1:0]; ALU_A = RegisterCtrl[2]; WRSel[1:0] = RegisterCtrl[4:3];
  //   WriteBackSel[2:0] = RegisterCtrl[7:5]

  // Notes on the sheet:
  //   Writeback
  //   Selector
  //   238
  //   内部レジスタ
  //   出力イネーブル付きバッファ541
  //   541
  //   139でイネーブルコントロール
  //   4to1 253
  //   ここはあらかじめ8本に減らしておくべき
  //   S Z C
  //   377
  //   175説 Jccの近く
  //   S Z C
endmodule

module CLK_GEN (
  input  CLK,
  input  Reset,
  output T1,
  output T2,
  output T3,
  output nRST
);

  wire and_1_out, d_ff_1_q, d_ff_2_q, d_ff_6_qn, not_1_out, not_2_out, not_3_out, not_4_out, not_5_out,
       not_6_out, not_7_out, not_8_out, not_9_out, PowerOnReset_q;

  not not_1 (not_1_out, CLK);
  not not_2 (not_2_out, Reset);
  D_Flip_Flop PowerOnReset (.clk(not_1_out), .D(1'b1), .Q(PowerOnReset_q));  // open: Qn, preset, en, reset
  D_Flip_Flop d_ff_1 (.clk(not_1_out), .D(1'b1), .Q(d_ff_1_q), .reset(not_3_out));  // open: Qn, preset, en
  not not_3 (not_3_out, and_1_out);
  and and_1 (and_1_out, not_2_out, PowerOnReset_q);
  D_Flip_Flop d_ff_2 (.clk(not_1_out), .D(d_ff_1_q), .Q(d_ff_2_q), .reset(not_4_out));  // open: Qn, preset, en
  not not_4 (not_4_out, and_1_out);
  not not_5 (not_5_out, not_1_out);
  D_Flip_Flop d_ff_3 (.clk(not_1_out), .D(d_ff_2_q), .Q(nRST), .reset(not_6_out));  // open: Qn, preset, en
  not not_6 (not_6_out, and_1_out);
  D_Flip_Flop d_ff_4 (.clk(not_5_out), .D(d_ff_6_qn), .Q(T1), .reset(not_7_out));  // open: Qn, preset, en
  not not_7 (not_7_out, nRST);
  D_Flip_Flop d_ff_5 (.clk(not_1_out), .D(T1), .Q(T2), .reset(not_8_out));  // open: Qn, preset, en
  not not_8 (not_8_out, nRST);
  D_Flip_Flop d_ff_6 (.clk(not_5_out), .D(T1), .Q(T3), .Qn(d_ff_6_qn), .reset(not_9_out));  // open: preset, en
  not not_9 (not_9_out, nRST);

  // Notes on the sheet:
  //   LogiSimのシミュレーションリセット対応
  //   74x3またはリセット部分を省略して7474x2
  //   Qの半クロック後
endmodule

module Equal14 (
  input  [13:0] In0,
  input  [13:0] In1,
  output Y
);

  wire [13:0] not_1_out, xor_1_out;

  assign not_1_out = ~xor_1_out;  // NOT_Gate not_1, 14 bits wide
  assign xor_1_out = In0 ^ In1;  // XOR_Gate xor_1, 14 bits wide
  and and_1 (Y, not_1_out[0], not_1_out[1], not_1_out[2], not_1_out[3], not_1_out[4], not_1_out[5], not_1_out[6], not_1_out[7], not_1_out[8], not_1_out[9], not_1_out[10], not_1_out[11], not_1_out[12], not_1_out[13]);
endmodule

module uROM (
  input  [7:0] OpeCode,
  input  Load,
  input  Update,
  output [11:0] STEP_MON,
  output [15:0] CtrlSignal
);

  wire not_1_out;

  not not_1 (not_1_out, Load);
  Counter #(.width(4), .max('hf)) _161 (
    .load(Load), .D(4'b0000), .count(not_1_out), .Q(STEP_MON[3:0]), .clk(Update));  // open: carry, clr
  Register _377 (.D(OpeCode), .en(Load), .Q(STEP_MON[11:4]), .clk(Update));  // open: clr
  // Probe on STEP_MON
  ROM #(.addrWidth(12), .dataWidth(16)) rom_1 (.addr(STEP_MON), .data(CtrlSignal));  // open: sel

  // Notes on the sheet:
  //   contents of rom_1 (hex, n*v repeats v):
  //   c000 15*0 4939 d0f9 14*0 4098 10f9 4098 4920 d0f9 11*0 4098 78 4920 d0f9 12*0 4929 d0f9 30*0 4959
  //   a8f 94a e6e 4921 d0f9 154*0 4999 10f9 4979 10f9 c0a0 11*0 4999 10f9 4979 10f9 c0c0 107*0 4959 a8f
  //   94a e6e 4941 5961 885 4921 d0f9 55*0 8808 c008 830*0 c92b 271*0 4999 10f9 4979 10f9 c0c0 107*0 80 60
  //   c0a0 13*0 80 60 c0c0 157*0 4999 10f9 4979 10f9 4941 5961 884 a8f 942 c6e c0a0 197*0 840 ca20 1278*0
  //   c520 256*0 40 664 684 4941 7981 864 c0e0 8*0 4018 d0f9 206*0 4959 10f9 a9f 744 c7e c0e0 10*0 d0f9
  //   15*0 c000 127*0 4999 10f9 4979 10f9 30d0 95a 8814 30d0 95b 8814 c0e0 37*0 4991 10d0 4971 10d0 c0e0
  //   43*0 4999 10f9 4979 10f9 c0e0
endmodule

module D_FF16 (
  input  [15:0] In,
  input  CLK,
  output [15:0] Out
);

  Register register_1 (.D(In[7:0]), .Q(Out[7:0]), .clk(CLK));  // open: en, clr
  Register register_2 (.D(In[15:8]), .Q(Out[15:8]), .clk(CLK));  // open: en, clr
endmodule

module D_FF8 (
  input  [7:0] In,
  input  CLK,
  input  OE,
  output [7:0] Out
);

  wire [7:0] register_1_q;

  Register register_1 (.D(In), .Q(register_1_q), .clk(CLK));  // open: en, clr
  assign Out = OE ? register_1_q : 8'bz;  // Controlled_Buffer controlled_buffer_1
endmodule

module ALU (
  input  [7:0] A,
  input  [7:0] B,
  input  Carry,
  input  [7:0] OpIn,
  input  SAR,
  output [7:0] LOutMon,
  output ZF,
  output [7:0] ALU_OUT,
  output Carry_2
);

  wire alu8a_1_cy, ext_1_cout, multiplexer_1_out, multiplexer_2_out, not_1_out, xor_1_out;
  wire [7:0] alu8a_1_y, ext_1_y;

  Multiplexer #(.disabled(0), .enable("false")) multiplexer_1 (
    .in0(1'b0), .in1(Carry), .out(multiplexer_1_out), .sel(OpIn[6]));
  xor xor_1 (xor_1_out, multiplexer_1_out, OpIn[5]);
  ALU8L alu8l_1 (.A(A), .B(B), .S(OpIn[3:0]), .Y(LOutMon));
  // Probe on OpIn[3:0]
  ALU8A alu8a_1 (.B(LOutMon), .A(A), .Cin(xor_1_out), .CY(alu8a_1_cy), .Y(alu8a_1_y));
  Ext ext_1 (.A(LOutMon), .Y(ext_1_y), .nThru(OpIn[7]), .SAR(SAR), .COut(ext_1_cout), .CIn(alu8a_1_cy));
  assign ALU_OUT = OpIn[4] ? ext_1_y : 8'bz;  // Controlled_Buffer controlled_buffer_1
  assign ALU_OUT = not_1_out ? alu8a_1_y : 8'bz;  // Controlled_Buffer controlled_buffer_2
  not not_1 (not_1_out, OpIn[4]);
  ZeroFlag zeroflag_1 (.A(ALU_OUT), .Y(ZF));
  Multiplexer #(.disabled(0), .enable("false")) multiplexer_2 (
    .in0(1'b0), .in1(ext_1_cout), .out(multiplexer_2_out), .sel(OpIn[4]));
  xor xor_2 (Carry_2, multiplexer_2_out, OpIn[5]);

  // Notes on the sheet:
  //   4078
endmodule

module INC_DEC16 (
  input  CarryIn,
  input  INC_DEC,
  input  [15:0] IN,
  output INC,
  output DEC,
  output [15:0] OUT
);

  wire inc_dec8_1_cout, not_1_out;

  not not_1 (not_1_out, INC_DEC);
  INC_DEC8 inc_dec8_1 (.INC_DEC(INC_DEC), .CI(CarryIn), .A(IN[7:0]), .Y(OUT[7:0]), .COut(inc_dec8_1_cout));
  INC_DEC8 inc_dec8_2 (.INC_DEC(INC_DEC), .CI(inc_dec8_1_cout), .A(IN[15:8]), .Y(OUT[15:8]));  // open: COut
  and and_1 (INC, CarryIn, not_1_out);
  and and_2 (DEC, CarryIn, INC_DEC);
endmodule

module INC_DEC8 (
  input  INC_DEC,
  input  CI,
  input  [7:0] A,
  output [7:0] Y,
  output COut
);

  wire and_1_out, and_2_out, and_3_out, and_4_out, and_5_out, and_6_out, and_7_out, and_8_out, and_9_out,
       and_10_out, and_11_out, and_12_out, and_13_out, and_14_out, and_15_out, and_16_out, multiplexer_1_out,
       multiplexer_2_out, multiplexer_3_out, multiplexer_4_out, multiplexer_5_out, multiplexer_6_out,
       multiplexer_7_out, nDEC;

  not not_1 (nDEC, INC_DEC);
  and and_1 (and_1_out, CI, A[0]);
  and and_2 (and_2_out, CI, ~A[0]);  // AND_Gate
  and and_3 (and_3_out, and_1_out, A[1]);
  and and_4 (and_4_out, and_2_out, ~A[1]);  // AND_Gate
  and and_5 (and_5_out, and_3_out, A[2]);
  and and_6 (and_6_out, and_4_out, ~A[2]);  // AND_Gate
  and and_7 (and_7_out, and_5_out, A[3]);
  and and_8 (and_8_out, and_6_out, ~A[3]);  // AND_Gate
  and and_9 (and_9_out, and_7_out, A[4]);
  and and_10 (and_10_out, and_8_out, ~A[4]);  // AND_Gate
  and and_11 (and_11_out, and_9_out, A[5]);
  and and_12 (and_12_out, and_10_out, ~A[5]);  // AND_Gate
  and and_13 (and_13_out, and_11_out, A[6]);
  and and_14 (and_14_out, and_12_out, ~A[6]);  // AND_Gate
  and and_15 (and_15_out, and_13_out, A[7]);
  and and_16 (and_16_out, and_14_out, ~A[7]);  // AND_Gate
  Multiplexer #(.disabled(0), .enable("false")) multiplexer_1 (
    .in0(and_1_out), .in1(and_2_out), .out(multiplexer_1_out), .sel(INC_DEC));
  Multiplexer #(.disabled(0), .enable("false")) multiplexer_2 (
    .in0(and_3_out), .in1(and_4_out), .out(multiplexer_2_out), .sel(INC_DEC));
  Multiplexer #(.disabled(0), .enable("false")) multiplexer_3 (
    .in0(and_5_out), .in1(and_6_out), .out(multiplexer_3_out), .sel(INC_DEC));
  Multiplexer #(.disabled(0), .enable("false")) multiplexer_4 (
    .in0(and_7_out), .in1(and_8_out), .out(multiplexer_4_out), .sel(INC_DEC));
  Multiplexer #(.disabled(0), .enable("false")) multiplexer_5 (
    .in0(and_9_out), .in1(and_10_out), .out(multiplexer_5_out), .sel(INC_DEC));
  Multiplexer #(.disabled(0), .enable("false")) multiplexer_6 (
    .in0(and_11_out), .in1(and_12_out), .out(multiplexer_6_out), .sel(INC_DEC));
  Multiplexer #(.disabled(0), .enable("false")) multiplexer_7 (
    .in0(and_13_out), .in1(and_14_out), .out(multiplexer_7_out), .sel(INC_DEC));
  Multiplexer #(.disabled(0), .enable("false")) multiplexer_8 (
    .in0(and_15_out), .in1(and_16_out), .out(COut), .sel(INC_DEC));
  xor xor_1 (Y[0], CI, A[0]);
  xor xor_2 (Y[1], multiplexer_1_out, A[1]);
  xor xor_3 (Y[2], multiplexer_2_out, A[2]);
  xor xor_4 (Y[3], multiplexer_3_out, A[3]);
  xor xor_5 (Y[4], multiplexer_4_out, A[4]);
  xor xor_6 (Y[5], multiplexer_5_out, A[5]);
  xor xor_7 (Y[6], multiplexer_6_out, A[6]);
  xor xor_8 (Y[7], multiplexer_7_out, A[7]);

  // Other names for the same wires on the sheet: DEC = INC_DEC
endmodule

module OP (
  input  [3:0] OPin,
  output [7:0] OpOut,
  output [3:0] OP,
  output FL,
  output SAR
);

  wire optable_1_sxt;

  OpTable optable_1 (
    .A2(OPin[3]), .A1(OPin[2]), .A0(OPin[1]), .D3(OP[3]), .M(OPin[0]), .D2(OP[2]), .D1(OP[1]), .D0(OP[0]),
    .MO(OpOut[4]), .Ci(OpOut[6]), .FL(FL), .CInv(OpOut[5]), .SXT(optable_1_sxt));
  and and_1 (SAR, OPin[0], OPin[1], OPin[2], OPin[3]);
  or or_1 (OpOut[7], optable_1_sxt, SAR);

  assign OpOut[3:0] = OP;
endmodule

module OpTable (
  input  A2,
  input  A1,
  input  A0,
  input  M,
  output D3,
  output D2,
  output D1,
  output D0,
  output MO,
  output Ci,
  output FL,
  output CInv,
  output SXT
);

  wire and_1_out, and_2_out, and_3_out, and_4_out, and_5_out, and_6_out, and_7_out, and_8_out, and_9_out,
       and_11_out, and_12_out, and_13_out, and_14_out, and_15_out, and_16_out, and_17_out, and_18_out,
       and_19_out, and_20_out, and_21_out, and_22_out, and_23_out, and_24_out, and_25_out, and_26_out,
       and_27_out, not_1_out, not_2_out, not_3_out, not_4_out, not_5_out, not_6_out, not_7_out, not_8_out,
       not_9_out, not_10_out, not_11_out, not_12_out, not_13_out, not_14_out, not_15_out, not_16_out,
       not_17_out, not_18_out, not_19_out, not_20_out, not_21_out, not_22_out, not_23_out, not_24_out,
       not_25_out, not_26_out, not_27_out, not_28_out, not_29_out, not_30_out, not_31_out, not_32_out,
       not_33_out, not_34_out, not_35_out, not_36_out, not_37_out, not_38_out, not_39_out, not_40_out,
       not_41_out, not_42_out;

  not not_1 (not_1_out, A1);
  and and_1 (and_1_out, not_1_out, not_2_out, M);
  not not_2 (not_2_out, A0);
  not not_3 (not_3_out, A2);
  and and_2 (and_2_out, not_3_out, A0, not_4_out);
  not not_4 (not_4_out, M);
  and and_3 (and_3_out, A1, A0, M);
  and and_4 (and_4_out, A2, not_5_out, not_6_out);
  not not_5 (not_5_out, A1);
  not not_6 (not_6_out, M);
  and and_5 (and_5_out, A2, not_7_out, not_8_out);
  not not_7 (not_7_out, A0);
  not not_8 (not_8_out, M);
  not not_9 (not_9_out, A2);
  not not_10 (not_10_out, A1);
  not not_11 (not_11_out, A1);
  not not_12 (not_12_out, M);
  not not_13 (not_13_out, A2);
  not not_14 (not_14_out, M);
  not not_15 (not_15_out, A0);
  not not_16 (not_16_out, M);
  not not_17 (not_17_out, A1);
  not not_18 (not_18_out, A0);
  not not_19 (not_19_out, A2);
  not not_20 (not_20_out, A1);
  not not_21 (not_21_out, A0);
  not not_22 (not_22_out, M);
  not not_23 (not_23_out, A2);
  not not_24 (not_24_out, M);
  not not_25 (not_25_out, A1);
  not not_26 (not_26_out, A0);
  not not_27 (not_27_out, A2);
  and and_6 (and_6_out, not_27_out, not_28_out);
  not not_28 (not_28_out, A1);
  not not_29 (not_29_out, A2);
  and and_7 (and_7_out, not_29_out, not_30_out, not_31_out);
  not not_30 (not_30_out, A0);
  not not_31 (not_31_out, M);
  not not_32 (not_32_out, A1);
  and and_8 (and_8_out, not_32_out, not_33_out);
  not not_33 (not_33_out, A0);
  and and_9 (and_9_out, A1, A0, M);
  and and_10 (Ci, A2, A1);
  not not_34 (not_34_out, A1);
  not not_35 (not_35_out, A0);
  not not_36 (not_36_out, M);
  not not_37 (not_37_out, A2);
  not not_38 (not_38_out, A1);
  not not_39 (not_39_out, A0);
  not not_40 (not_40_out, A0);
  not not_41 (not_41_out, A1);
  not not_42 (not_42_out, A2);
  or or_1 (D3, and_1_out, and_2_out, and_3_out, and_4_out, and_5_out);
  and and_11 (and_11_out, not_9_out, not_10_out, A0);
  and and_12 (and_12_out, not_11_out, A0, not_12_out);
  and and_13 (and_13_out, not_13_out, A1, not_14_out);
  and and_14 (and_14_out, A1, not_15_out, not_16_out);
  and and_15 (and_15_out, A2, not_17_out, not_18_out, M);
  and and_16 (and_16_out, not_19_out, A0);
  and and_17 (and_17_out, A0, M);
  and and_18 (and_18_out, A2, not_20_out, not_21_out, not_22_out);
  and and_19 (and_19_out, A2, A1, M);
  and and_20 (and_20_out, not_23_out, A1, not_24_out);
  or or_2 (D0, and_20_out, and_21_out, and_22_out);
  and and_21 (and_21_out, A2, not_25_out, A0, M);
  and and_22 (and_22_out, A2, A1, not_26_out, M);
  or or_3 (MO, and_6_out, and_7_out, and_8_out, and_9_out);
  and and_23 (and_23_out, not_34_out, not_35_out, not_36_out);
  or or_4 (FL, and_23_out, and_24_out, and_25_out);
  and and_24 (and_24_out, not_37_out, A1, A0, M);
  and and_25 (and_25_out, A2, not_38_out, not_39_out);
  and and_26 (and_26_out, A1, not_40_out, M);
  or or_5 (CInv, and_26_out, and_27_out);
  and and_27 (and_27_out, A2, not_41_out, A0, M);
  and and_28 (SXT, not_42_out, A1, A0, M);
  or or_6 (D2, and_11_out, and_12_out, and_13_out, and_14_out, and_15_out);
  or or_7 (D1, and_16_out, and_17_out, and_18_out, and_19_out);
endmodule

module Ext (
  input  [7:0] A,
  input  CIn,
  input  SAR,
  input  nThru,
  output [7:0] Y,
  output COut
);

  Multiplexer #(.select(2), .width(8), .disabled(0), .enable("false")) multiplexer_1 (
    .in0(A), .in1({8{A[7]}}), .in2(A), .in3({CIn, A[7:1]}), .out(Y), .sel({SAR, nThru}));
  Multiplexer #(.disabled(0), .enable("false")) multiplexer_2 (.in0(CIn), .in1(A[0]), .out(COut), .sel(nThru));
endmodule

module ALU8L (
  input  [7:0] A,
  input  [7:0] B,
  input  [3:0] S,
  output [7:0] Y
);

  // Probe on S
  Multiplexer #(.select(2), .disabled(0), .enable("false")) multiplexer_1 (
    .in0(S[0]), .in1(S[1]), .in2(S[2]), .in3(S[3]), .out(Y[4]), .sel({B[4], A[4]}));
  Multiplexer #(.select(2), .disabled(0), .enable("false")) multiplexer_2 (
    .in0(S[0]), .in1(S[1]), .in2(S[2]), .in3(S[3]), .out(Y[5]), .sel({B[5], A[5]}));
  Multiplexer #(.select(2), .disabled(0), .enable("false")) multiplexer_3 (
    .in0(S[0]), .in1(S[1]), .in2(S[2]), .in3(S[3]), .out(Y[6]), .sel({B[6], A[6]}));
  Multiplexer #(.select(2), .disabled(0), .enable("false")) multiplexer_4 (
    .in0(S[0]), .in1(S[1]), .in2(S[2]), .in3(S[3]), .out(Y[7]), .sel({B[7], A[7]}));
  Multiplexer #(.select(2), .disabled(0), .enable("false")) multiplexer_5 (
    .in0(S[0]), .in1(S[1]), .in2(S[2]), .in3(S[3]), .out(Y[0]), .sel({B[0], A[0]}));
  Multiplexer #(.select(2), .disabled(0), .enable("false")) multiplexer_6 (
    .in0(S[0]), .in1(S[1]), .in2(S[2]), .in3(S[3]), .out(Y[1]), .sel({B[1], A[1]}));
  Multiplexer #(.select(2), .disabled(0), .enable("false")) multiplexer_7 (
    .in0(S[0]), .in1(S[1]), .in2(S[2]), .in3(S[3]), .out(Y[2]), .sel({B[2], A[2]}));
  Multiplexer #(.select(2), .disabled(0), .enable("false")) multiplexer_8 (
    .in0(S[0]), .in1(S[1]), .in2(S[2]), .in3(S[3]), .out(Y[3]), .sel({B[3], A[3]}));

  // Notes on the sheet:
  //   F16
  //   F16
endmodule

module ALU4A (
  input  [3:0] B,
  input  [3:0] A,
  input  CIn,
  output COut,
  output [3:0] Y
);

  wire and_1_out, and_2_out, and_3_out, and_4_out, and_5_out, and_6_out, and_7_out, and_8_out, and_9_out,
       and_10_out, and_11_out, and_12_out, and_13_out, and_14_out, or_2_out, or_3_out, or_4_out, xor_1_out,
       xor_2_out, xor_3_out, xor_4_out;

  xor xor_1 (xor_1_out, B[3], A[3]);
  and and_1 (and_1_out, B[3], A[3]);
  xor xor_2 (xor_2_out, B[2], A[2]);
  and and_2 (and_2_out, B[2], A[2]);
  xor xor_3 (xor_3_out, B[1], A[1]);
  and and_3 (and_3_out, B[1], A[1]);
  xor xor_4 (xor_4_out, B[0], A[0]);
  and and_4 (and_4_out, B[0], A[0]);
  and and_5 (and_5_out, xor_1_out, and_2_out);
  and and_6 (and_6_out, xor_1_out, xor_2_out, and_3_out);
  and and_7 (and_7_out, xor_1_out, xor_2_out, xor_3_out, and_4_out);
  and and_8 (and_8_out, xor_1_out, xor_2_out, xor_3_out, xor_4_out, CIn);
  and and_9 (and_9_out, xor_2_out, and_3_out);
  and and_10 (and_10_out, xor_2_out, xor_3_out, and_4_out);
  and and_11 (and_11_out, xor_2_out, xor_3_out, xor_4_out, CIn);
  and and_12 (and_12_out, xor_3_out, and_4_out);
  and and_13 (and_13_out, xor_3_out, xor_4_out, CIn);
  and and_14 (and_14_out, xor_4_out, CIn);
  or or_1 (COut, and_1_out, and_5_out, and_6_out, and_7_out, and_8_out);
  or or_2 (or_2_out, and_2_out, and_9_out, and_10_out, and_11_out);
  or or_3 (or_3_out, and_3_out, and_12_out, and_13_out);
  or or_4 (or_4_out, and_4_out, and_14_out);
  xor xor_5 (Y[3], xor_1_out, or_2_out);
  xor xor_6 (Y[2], xor_2_out, or_3_out);
  xor xor_7 (Y[1], xor_3_out, or_4_out);
  xor xor_8 (Y[0], xor_4_out, CIn);
endmodule

module ALU8A (
  input  [7:0] B,
  input  [7:0] A,
  input  Cin,
  output CY,
  output [7:0] Y
);

  wire alu4a_2_cout;

  ALU4A alu4a_1 (.B(B[7:4]), .A(A[7:4]), .CIn(alu4a_2_cout), .COut(CY), .Y(Y[7:4]));
  ALU4A alu4a_2 (.B(B[3:0]), .A(A[3:0]), .CIn(Cin), .COut(alu4a_2_cout), .Y(Y[3:0]));
endmodule

module ZeroFlag (
  input  [7:0] A,
  output Y
);

  nor nor_1 (Y, A[0], A[1], A[2], A[3], A[4], A[5], A[6], A[7]);
endmodule

module MUX4to1x8 (
  input  [7:0] D0,
  input  [7:0] D1,
  input  [7:0] D2,
  input  [7:0] D3,
  input  [1:0] Sel,
  output [7:0] Y,
  output I0,
  output I1,
  output I2,
  output I3
);

  Multiplexer #(.select(2), .width(8), .enable("false")) multiplexer_1 (
    .in0(D0), .in1(D1), .in2(D2), .in3(D3), .out(Y), .sel(Sel));
  Demultiplexer #(.select(2), .disabled(0), .enable("false")) demultiplexer_1 (
    .out0(I0), .out1(I1), .out2(I2), .out3(I3), .in(1'b1), .sel(Sel));

  // Notes on the sheet:
  //   139
endmodule

module MUX4to1x16 (
  input  [15:0] D0,
  input  [15:0] D1,
  input  [15:0] D2,
  input  [15:0] D3,
  input  [1:0] Sel,
  output [15:0] Y,
  output I0,
  output I1,
  output I2,
  output I3
);

  Multiplexer #(.select(2), .width(16), .enable("false")) multiplexer_1 (
    .in0(D0), .in1(D1), .in2(D2), .in3(D3), .out(Y), .sel(Sel));
  Demultiplexer #(.select(2), .disabled(0), .enable("false")) demultiplexer_1 (
    .out0(I0), .out1(I1), .out2(I2), .out3(I3), .in(1'b1), .sel(Sel));

  // Notes on the sheet:
  //   139
endmodule
