// Logisim project CPU298_parts.circ as structural Verilog
module PartsPlacement (
);

  Extern extern_1 ();
  _20pin _377_BusBuffer ();
  _20pin u_20pin_1 ();
  _20pin u_20pin_2 ();
  _20pin u_20pin_3 ();
  _24pin inc8 ();
  _24pin inc8_2 ();
  _600mil40pin _27C1024 ();
  _20pin _574 ();
  _20pin _574_2 ();
  _20pin _574_3 ();
  _20pin _574_4 ();
  _20pin _574_5 ();
  _20pin _574_6 ();
  _20pin _574_7 ();
  _20pin _574_8 ();
  _20pin _574_9 ();
  _20pin _574_10 ();
  _14pin _283 ();
  _20pin u_20pin_4 ();
endmodule

module PC_298 (
);

  wire Reset_out;
  wire [7:0] keyboard_1_data;
  wire [11:0] system_1_console_out;

  Button Reset (.out(Reset_out));
  System system_1 (.ResetIn(Reset_out), .Console_OUT(system_1_console_out), .Console_IN(keyboard_1_data));
  TTY #(.rows(25), .cols(80)) tty_1 (
    .data(system_1_console_out[6:0]), .clk(system_1_console_out[7]), .we(system_1_console_out[8]),
    .clr(system_1_console_out[9]));
  Keyboard keyboard_1 (
    .clk(system_1_console_out[7]), .re(system_1_console_out[10]), .clr(system_1_console_out[11]),
    .avail(keyboard_1_data[7]), .data(keyboard_1_data[6:0]));

  // Notes on the sheet:
  //   Key Input
endmodule

module System (
  input  ResetIn,
  input  [7:0] Console_IN,
  output [11:0] Console_OUT
);

  wire and_1_out, Clock_out, decoder_1_out0, decoder_1_out1, decoder_1_out2, decoder_1_out3, equal14_1_y,
       n298_core_1_read, n298_core_1_s0, n298_core_1_s1, n298_core_1_write, not_1_out, not_2_out, not_4_out,
       or_1_out, or_2_out;
  wire [7:0] n298_core_1_dataout, register_1_q;
  wire [15:0] n298_core_1_addressout;

  Clock Clock (.out(Clock_out));
  _298_CORE u_298_core_1 (
    .Reset(ResetIn), .DataOut(n298_core_1_dataout), .DataIn(n298_core_1_dataout), .Read(n298_core_1_read),
    .AddressOut(n298_core_1_addressout), .CLK(Clock_out), .Write(n298_core_1_write), .S0(n298_core_1_s0),
    .S1(n298_core_1_s1));
  // Probe on n298_core_1_dataout
  // Probe on n298_core_1_addressout
  not not_1 (not_1_out, n298_core_1_write);
  or or_1 (or_1_out, n298_core_1_read, n298_core_1_write);
  Pull_Resistor pull_resistor_1 (.node(n298_core_1_dataout));
  Pull_Resistor pull_resistor_2 (.node(n298_core_1_addressout));
  and and_1 (and_1_out, or_1_out, not_2_out);
  Equal14 equal14_1 (.In0(n298_core_1_addressout[15:2]), .In1(14'h3f84), .Y(equal14_1_y));
  Decoder #(.select(2), .disabled(0)) decoder_1 (
    .out0(decoder_1_out0), .out1(decoder_1_out1), .out2(decoder_1_out2), .out3(decoder_1_out3),
    .sel(n298_core_1_addressout[15:14]), .en(and_1_out));
  not not_2 (not_2_out, equal14_1_y);
  and and_2 (Console_OUT[8], equal14_1_y, not_1_out);
  and and_3 (Console_OUT[10], equal14_1_y, n298_core_1_read);
  assign n298_core_1_dataout = Console_OUT[10] ? register_1_q : 8'bz;  // Controlled_Buffer controlled_buffer_1
  ROM #(.addrWidth(14)) rom_1 (.addr(n298_core_1_addressout[13:0]), .data(n298_core_1_dataout), .sel(decoder_1_out0));
  assign Console_OUT[6:0] = Console_OUT[8] ? n298_core_1_dataout[6:0] : 7'bz;  // Controlled_Buffer controlled_buffer_2
  not not_3 (Console_OUT[7], not_4_out);
  not not_4 (not_4_out, or_2_out);
  or or_2 (or_2_out, Console_OUT[8], Console_OUT[10]);
  RAM #(.addrWidth(14)) ram_1 (
    .addr(n298_core_1_addressout[13:0]), .data(n298_core_1_dataout), .sel(decoder_1_out1), .clk(not_1_out),
    .ld(n298_core_1_read), .clr(1'b0));
  Register register_1 (.D(Console_IN), .en(Console_OUT[10]), .Q(register_1_q), .clk(Console_OUT[10]), .clr(ResetIn));
  RAM #(.addrWidth(14)) ram_2 (
    .addr(n298_core_1_addressout[13:0]), .data(n298_core_1_dataout), .sel(decoder_1_out2), .clk(not_1_out),
    .ld(n298_core_1_read), .clr(1'b0));
  RAM #(.addrWidth(14)) ram_3 (
    .addr(n298_core_1_addressout[13:0]), .data(n298_core_1_dataout), .sel(decoder_1_out3), .clk(not_1_out),
    .ld(n298_core_1_read), .clr(1'b0));

  assign {Console_OUT[11], Console_OUT[9]} = {2{ResetIn}};

  // Other names for the same wires on the sheet: Reset = ResetIn

  // Notes on the sheet:
  //   ADDR Decoder
  //   ROM0 0000-3FFF
  //   contents of rom_1 (hex, n*v repeats v):
  //   1e 4 f8 7 0 ee fb fb fd bf e5 4 d7 fe 2 0 ee fe 7c 0 f 0 a5 8 e5 fb d6 9 fe e9 ff 48 65 6c 6c 6f 0
  //   6e 48 65 6c 6c 6f 21*0 8 5a 28 0 80 17*0 76 553*0 34 413*0 fe 231*0 76 2553*0 f8 aa 8478*0 6e
  //   RAM0 4000-7FFF
  //   RAM1 8000-BFFF
  //   RAM2 C000-FFFF
endmodule

module _298_CORE (
  input  [7:0] DataIn,
  input  CLK,
  input  Reset,
  output [7:0] DataOut,
  output [15:0] AddressOut,
  output Write,
  output Read,
  output S0,
  output S1
);

  wire and_1_out, and_2_out, and_3_out, and_4_out, CLK_t, d_ff_1_qn, d_ff_2_qn, E, nRST, or_1_out, Q, Resume,
       sequencer_1_jump_op, sequencer_1_loadopecode, sequencer_1_ndo_jump, sequencer_1_stageclock,
       sequencer_1_stepupdate, \sequencer_1_μrom_address_clk ;
  wire [1:0] sequencer_1_exbuscontrol;
  wire [2:0] executer_1_flagregisterout;
  wire [5:0] sequencer_1_aluop;
  wire [7:0] buffer_1_out, executer_1_dataout, sequencer_1_dataout, sequencer_1_executercontrol;
  wire [11:0] sequencer_1_step_monitor;
  wire [15:0] executer_1_addrout;

  CLK_GEN2 clk_gen2_1 (.CLK(CLK), .Reset(Reset), .Q(Q), .E(E), .nRST(nRST));
  Executer executer_1 (
    .DataOut(executer_1_dataout), .FlagRegisterOut(executer_1_flagregisterout), .E(E),
    .AddrOut(executer_1_addrout), .DataIn(sequencer_1_dataout), .RegisterCtrl(sequencer_1_executercontrol),
    .STEP(sequencer_1_step_monitor), .ALUOP(sequencer_1_aluop), .Q(Q), .CLK(CLK_t), .Resume(Resume));
  // Probe on sequencer_1_executercontrol
  // Probe on sequencer_1_aluop
  Sequencer sequencer_1 (
    .FlagIn(executer_1_flagregisterout), .Q(Q), .E(E), .nReset(nRST), .DataIn(buffer_1_out),
    .ExecuterControl(sequencer_1_executercontrol), .ExBusControl(sequencer_1_exbuscontrol),
    .STEP_Monitor(sequencer_1_step_monitor), .DataOut(sequencer_1_dataout), .Stage_1(S1), .Stage_0(S0),
    .StepUpdate(sequencer_1_stepupdate), .JUMP_OP(sequencer_1_jump_op), .nDO_JUMP(sequencer_1_ndo_jump),
    .StageClock(sequencer_1_stageclock), .LoadOpeCode(sequencer_1_loadopecode),
    .\μROM_Address_CLK (\sequencer_1_μrom_address_clk ), .ALUOP(sequencer_1_aluop));
  assign buffer_1_out = DataIn;  // Buffer buffer_1, 8 bits wide
  D_Latch8 d_latch8_1 (.In(executer_1_dataout), .LE(or_1_out), .OE(and_1_out), .Out(DataOut));
  D_Latch16 d_latch16_1 (.In(executer_1_addrout), .Out(AddressOut), .LE(or_1_out));
  or or_1 (or_1_out, E, Q);
  and and_1 (and_1_out, or_1_out, and_3_out);
  and and_2 (and_2_out, E, ~Q);  // AND_Gate
  and and_3 (and_3_out, ~sequencer_1_exbuscontrol[0], sequencer_1_exbuscontrol[1]);  // AND_Gate
  and and_4 (and_4_out, sequencer_1_exbuscontrol[0], ~sequencer_1_exbuscontrol[1]);  // AND_Gate
  D_Flip_Flop d_ff_1 (.clk(Q), .D(and_3_out), .Qn(d_ff_1_qn), .reset(and_2_out));  // open: Q, preset, en
  not not_1 (Write, d_ff_1_qn);
  D_Flip_Flop d_ff_2 (.clk(Q), .D(and_4_out), .Qn(d_ff_2_qn), .reset(and_2_out));  // open: Q, preset, en
  not not_2 (Read, d_ff_2_qn);

  // Notes on the sheet:
  //   Reset: pull=up
  //   Q or E がラッチイネーブル
  //   HCT541
  //   373/573
  //   OE付きトランスペアレントラッチ
  //   DataBus_In
  //   DataBus_Out
  //   AddressBus
  //   Q↓からE↓までの間クリア
endmodule

module Sequencer (
  input  [7:0] DataIn,
  input  nReset,
  input  Q,
  input  E,
  input  [2:0] FlagIn,
  output [11:0] STEP_Monitor,
  output \μROM_Address_CLK ,
  output [7:0] ExecuterControl,
  output LoadOpeCode,
  output [5:0] ALUOP,
  output [1:0] ExBusControl,
  output [7:0] DataOut,
  output StepUpdate,
  output StageClock,
  output Stage_1,
  output JUMP_OP,
  output Stage_0,
  output nDO_JUMP
);

  wire and_1_out, and_2_out, and_3_out, and_5_out, d_ff_1_q, multiplexer_2_out, nE, nor_1_out, not_3_out,
       not_4_out, not_5_out, not_6_out, not_7_out, not_8_out, not_9_out, not_10_out, not_11_out, not_12_out,
       nQ, or_2_out, Stage_Bit0_qn, Stage_Bit1_qn;
  wire [3:0] JUMP_OP_t;
  wire [7:0] IR_q, multiplexer_1_out;
  wire [15:0] urom_a_1_ctrlsignal;

  not not_1 (nQ, Q);
  not not_2 (nE, E);
  // Probe on {DataIn[7:4], JUMP_OP_t}
  Register IR (.D({DataIn[7:4], JUMP_OP_t}), .en(d_ff_1_q), .Q(IR_q), .clk(E));  // open: clr
  D_Flip_Flop d_ff_1 (.clk(Q), .D(and_1_out), .Q(d_ff_1_q), .reset(not_3_out));  // open: Qn, preset, en
  not not_3 (not_3_out, nReset);
  and and_1 (and_1_out, ~STEP_Monitor[0], Stage_Bit1_qn, Stage_0);  // AND_Gate
  and and_2 (and_2_out, Stage_0, Stage_Bit1_qn);
  and and_3 (and_3_out, Stage_1, Stage_Bit0_qn);
  D_Flip_Flop Stage_Bit1 (
    .clk(StageClock), .D(and_2_out), .Q(Stage_1), .Qn(Stage_Bit1_qn), .reset(not_4_out));  // open: preset, en
  D_Flip_Flop Stage_Bit0 (
    .clk(StageClock), .D(Stage_Bit0_qn), .Q(Stage_0), .Qn(Stage_Bit0_qn), .reset(not_4_out));  // open: preset, en
  not not_4 (not_4_out, nReset);
  Multiplexer #(.width(8), .disabled(0), .enable("false")) multiplexer_1 (
    .in0({7'b1110000, Stage_0}), .in1(IR_q), .out(multiplexer_1_out), .sel(and_3_out));
  // Probe on multiplexer_1_out
  or or_1 (\μROM_Address_CLK , E, nor_1_out);
  D_Flip_Flop StepControl (.clk(Q), .D(StepUpdate), .Q(LoadOpeCode), .preset(not_5_out));  // open: Qn, en, reset
  not not_5 (not_5_out, nReset);
  D_Flip_Flop Stage_Control (.clk(nE), .D(StepUpdate), .Qn(StageClock), .reset(not_6_out));  // open: Q, preset, en
  not not_6 (not_6_out, nor_1_out);
  not not_7 (not_7_out, nReset);
  nor nor_1 (nor_1_out, not_7_out, Q);
  // Probe on STEP_Monitor
  uROM_A urom_a_1 (
    .OpeCode(multiplexer_1_out), .Load(LoadOpeCode), .Update(\μROM_Address_CLK ), .STEP_MON(STEP_Monitor),
    .CtrlSignal(urom_a_1_ctrlsignal));
  and and_4 (StepUpdate, urom_a_1_ctrlsignal[14], urom_a_1_ctrlsignal[15]);
  // Probe on urom_a_1_ctrlsignal
  not not_8 (not_8_out, FlagIn[0]);
  not not_9 (not_9_out, FlagIn[1]);
  or or_2 (or_2_out, FlagIn[0], FlagIn[1]);
  not not_10 (not_10_out, or_2_out);
  not not_11 (not_11_out, FlagIn[2]);
  not not_12 (not_12_out, nReset);
  and and_5 (and_5_out, DataIn[5], DataIn[6], DataIn[7]);
  Multiplexer #(.select(3), .disabled(0), .enable("false")) multiplexer_2 (
    .in0(not_8_out), .in1(FlagIn[0]), .in2(not_9_out), .in3(FlagIn[1]), .in4(or_2_out), .in5(not_10_out),
    .in6(not_11_out), .in7(FlagIn[2]), .out(multiplexer_2_out), .sel(DataIn[2:0]));
  Register #(.width(16)) Ctrl_signal_register (
    .D(urom_a_1_ctrlsignal), .Q({ExBusControl, ALUOP, ExecuterControl}), .clk(nE), .clr(not_12_out));  // open: en
  and and_6 (JUMP_OP, ~DataIn[3], ~DataIn[4], and_5_out);  // AND_Gate
  not not_13 (nDO_JUMP, multiplexer_2_out);
  Multiplexer #(.width(4), .disabled(0), .enable("false")) multiplexer_3 (
    .in0(DataIn[3:0]), .in1({3'b111, nDO_JUMP}), .out(JUMP_OP_t), .sel(JUMP_OP));

  assign DataOut = DataIn;

  // Other names for the same wires on the sheet: CY = FlagIn[0]; ZF = FlagIn[1]; SF = FlagIn[2];
  //   Step[11:0] = STEP_Monitor

  // Notes on the sheet:
  //   nReset: pull=up
  //   Fetch Opecode
  //   377 clken
  //   実行ステージ以外のときは0xEXにする
  //   μROM_IDX
  //   リセット時の初期化
  //   通常E↑で変化する
  //   354
  //   HCT273 AsyncReset
  //   Jcc Detector
  //   11
endmodule

module Executer (
  input  Q,
  input  E,
  input  [7:0] DataIn,
  input  [11:0] STEP,
  input  [5:0] ALUOP,
  input  [7:0] RegisterCtrl,
  output [2:0] FlagRegisterOut,
  output CLK,
  output Resume,
  output [7:0] DataOut,
  output [15:0] AddrOut
);

  wire and_1_out, and_2_out, decoder_1_out0, decoder_1_out1, decoder_1_out2, decoder_1_out3, decoder_1_out4,
       decoder_1_out5, decoder_1_out6, decoder_1_out7, inc_dec16_1_dec, inc_dec16_1_inc, mux4to1x8_1_i0,
       mux4to1x8_1_i1, mux4to1x8_1_i2, mux4to1x8_1_i3, mux4to1x16_1_i0, mux4to1x16_1_i1, mux4to1x16_1_i2,
       mux4to1x16_1_i3, not_1_out, not_2_out, op_1_ext, op_1_fl, op_1_nbthru;
  wire [1:0] alu_1_carry_2;
  wire [3:0] op_1_op;
  wire [7:0] A_q, alu_1_alu_out, alu_1_loutmon, controlled_buffer_1_out, H_q, L_q, mux4to1x8_1_y, op_1_opout,
       sxt_1_y, W_q;
  wire [15:0] mux4to1x16_1_y, PC_q, X_q, Y_q;

  // Probe on STEP
  and and_1 (and_1_out, ~ALUOP[4], ALUOP[5]);  // AND_Gate
  // Probe on DataIn
  // Probe on RegisterCtrl[7:5]
  and and_2 (and_2_out, Q, E);
  Decoder #(.select(3), .disabled(0)) decoder_1 (
    .out0(decoder_1_out0), .out1(decoder_1_out1), .out2(decoder_1_out2), .out3(decoder_1_out3),
    .out4(decoder_1_out4), .out5(decoder_1_out5), .out6(decoder_1_out6), .out7(decoder_1_out7),
    .sel(RegisterCtrl[7:5]), .en(and_2_out));
  Register A (.D(DataOut), .Q(A_q), .clk(decoder_1_out1));  // open: en, clr
  assign controlled_buffer_1_out = not_1_out ? A_q : 8'bz;  // Controlled_Buffer controlled_buffer_1
  Register W (.D(DataOut), .Q(W_q), .clk(decoder_1_out2));  // open: en, clr
  Register H (.D(DataOut), .Q(H_q), .clk(decoder_1_out3));  // open: en, clr
  Register L (.D(DataOut), .Q(L_q), .clk(decoder_1_out4));  // open: en, clr
  Register #(.width(16)) X (.D(AddrOut), .Q(X_q), .clk(decoder_1_out5));  // open: en, clr
  Register #(.width(16)) Y (.D(AddrOut), .Q(Y_q), .clk(decoder_1_out6));  // open: en, clr
  Register #(.width(16)) PC (.D(AddrOut), .Q(PC_q), .clk(decoder_1_out7));  // open: en, clr
  assign controlled_buffer_1_out = RegisterCtrl[2] ? W_q : 8'bz;  // Controlled_Buffer controlled_buffer_2
  not not_1 (not_1_out, RegisterCtrl[2]);
  // Probe on DataOut
  MUX4to1x16 mux4to1x16_1 (
    .D0({H_q, L_q}), .D1(X_q), .D2(Y_q), .D3(PC_q), .Sel(RegisterCtrl[4:3]), .Y(mux4to1x16_1_y),
    .I0(mux4to1x16_1_i0), .I1(mux4to1x16_1_i1), .I2(mux4to1x16_1_i2), .I3(mux4to1x16_1_i3));
  // Probe on AddrOut
  // Probe on controlled_buffer_1_out
  MUX4to1x8 mux4to1x8_1 (
    .D0(W_q), .D1(DataIn), .D2(AddrOut[15:8]), .D3(AddrOut[7:0]), .Sel(RegisterCtrl[1:0]), .Y(mux4to1x8_1_y),
    .I0(mux4to1x8_1_i0), .I1(mux4to1x8_1_i1), .I2(mux4to1x8_1_i2), .I3(mux4to1x8_1_i3));
  // Probe on mux4to1x8_1_y
  // Probe on mux4to1x16_1_y
  OP op_1 (
    .OPin(ALUOP[3:0]), .OP(op_1_op), .OpOut(op_1_opout), .FL(op_1_fl), .E(E), .nBThru(op_1_nbthru),
    .EXT(op_1_ext));
  // Probe on op_1_op
  Multiplexer #(.width(8), .disabled(0), .enable("false")) multiplexer_1 (
    .in0(mux4to1x8_1_y), .in1(sxt_1_y), .out(DataOut), .sel(op_1_nbthru));
  INC_DEC16 inc_dec16_1 (
    .IN(mux4to1x16_1_y), .OUT(AddrOut), .INC_DEC(ALUOP[5]), .CI(ALUOP[4]), .INC(inc_dec16_1_inc),
    .DEC(inc_dec16_1_dec));
  // Probe on alu_1_loutmon
  ALU alu_1 (
    .A(controlled_buffer_1_out), .Carry_2(alu_1_carry_2[0]), .ALU_OUT(alu_1_alu_out), .ZF(alu_1_carry_2[1]),
    .B(mux4to1x8_1_y), .LOutMon(alu_1_loutmon), .OpIn(op_1_opout), .Carry(FlagRegisterOut[0]));
  not not_2 (not_2_out, op_1_nbthru);
  SXT sxt_1 (.A(alu_1_alu_out), .Thru(op_1_ext), .OE(not_2_out), .Y(sxt_1_y));
  Register #(.width(3)) Flag (
    .D({alu_1_alu_out[7], alu_1_carry_2}), .Q(FlagRegisterOut), .clk(op_1_fl));  // open: en, clr
  Button ManualClock (.out(CLK));
  Button u_Resume (.out(Resume));

  // Other names for the same wires on the sheet: ALUOP_t[3:0] = ALUOP[3:0]; ADDR[1:0] = ALUOP[5:4];
  //   CarryFlag = FlagRegisterOut[0]; ALU_B[1:0] = RegisterCtrl[1:0]; ALU_A = RegisterCtrl[2];
  //   WRSel[1:0] = RegisterCtrl[4:3]; WriteBackSel[2:0] = RegisterCtrl[7:5]

  // Notes on the sheet:
  //   Writeback
  //   Selector
  //   238
  //   出力イネーブル付き574
  //   541
  //   4to1 153
  //   139
  //   DBUS-Thru出したい
  //   /BThru
  //   377
  //   175説 Jccの近く
endmodule

module CLK_GEN2 (
  input  CLK,
  input  Reset,
  output Q,
  output E,
  output nRST
);

  wire and_1_out, d_ff_1_q, d_ff_1_qn, d_ff_3_qn, not_1_out, not_2_out, not_3_out, not_4_out, not_5_out,
       not_6_out, not_7_out, PowerOnReset_q;

  not not_1 (not_1_out, CLK);
  not not_2 (not_2_out, Reset);
  not not_3 (not_3_out, and_1_out);
  D_Flip_Flop PowerOnReset (.clk(not_1_out), .D(1'b1), .Q(PowerOnReset_q));  // open: Qn, preset, en, reset
  D_Flip_Flop d_ff_1 (.clk(not_1_out), .D(1'b0), .Q(d_ff_1_q), .Qn(d_ff_1_qn), .preset(not_3_out));  // open: en, reset
  not not_4 (not_4_out, and_1_out);
  and and_1 (and_1_out, not_2_out, PowerOnReset_q);
  not not_5 (not_5_out, not_1_out);
  D_Flip_Flop d_ff_2 (.clk(not_1_out), .D(d_ff_1_q), .Qn(nRST), .preset(not_4_out));  // open: Q, en, reset
  not not_6 (not_6_out, nRST);
  D_Flip_Flop d_ff_3 (.clk(not_5_out), .D(Q), .Q(E), .Qn(d_ff_3_qn), .reset(not_6_out));  // open: preset, en
  not not_7 (not_7_out, nRST);
  D_Flip_Flop d_ff_4 (.clk(not_5_out), .D(d_ff_3_qn), .Q(Q), .reset(not_7_out));  // open: Qn, preset, en

  // Notes on the sheet:
  //   LogiSimのシミュレーションリセット対応
endmodule

module D_Latch16 (
  input  [15:0] In,
  input  LE,
  output [15:0] Out
);

  wire [7:0] register_1_q, register_2_q;

  Register register_1 (.D(In[7:0]), .Q(register_1_q), .clk(LE));  // open: en, clr
  Register register_2 (.D(In[15:8]), .Q(register_2_q), .clk(LE));  // open: en, clr
  Multiplexer #(.width(16), .disabled(0), .enable("false")) multiplexer_1 (
    .in0(In), .in1({register_2_q, register_1_q}), .out(Out), .sel(LE));
endmodule

module D_Latch8 (
  input  [7:0] In,
  input  LE,
  input  OE,
  output [7:0] Out
);

  wire [7:0] multiplexer_1_out, register_1_q;

  Register register_1 (.D(In), .Q(register_1_q), .clk(LE));  // open: en, clr
  Multiplexer #(.width(8), .disabled(0), .enable("false")) multiplexer_1 (
    .in0(In), .in1(register_1_q), .out(multiplexer_1_out), .sel(LE));
  assign Out = OE ? multiplexer_1_out : 8'bz;  // Controlled_Buffer controlled_buffer_1
endmodule

module uROM_A (
  input  [7:0] OpeCode,
  input  Load,
  input  Update,
  output [11:0] STEP_MON,
  output [15:0] CtrlSignal
);

  wire not_1_out;

  not not_1 (not_1_out, Load);
  Counter #(.width(4), .max('hf)) _161 (
    .load(Load), .D(4'b0000), .count(not_1_out), .Q(STEP_MON[3:0]), .clk(Update));  // open: carry, clr
  Register _377 (.D(OpeCode), .en(Load), .Q(STEP_MON[11:4]), .clk(Update));  // open: clr
  // Probe on STEP_MON
  ROM #(.addrWidth(12), .dataWidth(16)) rom_1 (.addr(STEP_MON), .data(CtrlSignal));  // open: sel

  // Notes on the sheet:
  //   contents of rom_1 (hex, n*v repeats v):
  //   c001 31*0 8808 c008 94*0 4939 d0f9 94*0 4959 a8f 94a e6e 4921 d0f9 250*0 4959 a8f 94a e6e 4941 5961
  //   885 4921 d0f9 151*0 4999 10f9 4979 10f9 c0a0 635*0 c92b 271*0 4999 10f9 4979 10f9 c0c0 107*0 80 60
  //   c0a0 13*0 80 60 c0c0 157*0 999 10f9 979 10f9 941 a8f 942 c6e c0a0 199*0 840 ca20 1278*0 c520 256*0
  //   80 60 c0e0 12*0 4018 d0f9 206*0 4959 10f9 a9f 744 c7e c0e0 10*0 d0f9 15*0 c000 127*0 4999 10f9 4979
  //   10f9 30d0 95a 8814 30d0 95b 8814 c0e0 37*0 4991 10d0 4971 10d0 c0e0 43*0 4999 10f9 4979 10f9 c0e0
endmodule

module INC_DEC16 (
  input  CI,
  input  INC_DEC,
  input  [15:0] IN,
  output INC,
  output DEC,
  output [15:0] OUT
);

  wire inc_dec8_1_cout, not_1_out;

  not not_1 (not_1_out, INC_DEC);
  INC_DEC8 inc_dec8_1 (.nThru(CI), .INC_DEC(INC_DEC), .CI(CI), .A(IN[7:0]), .Y(OUT[7:0]), .COut(inc_dec8_1_cout));
  INC_DEC8 inc_dec8_2 (.nThru(CI), .INC_DEC(INC_DEC), .CI(inc_dec8_1_cout), .A(IN[15:8]), .Y(OUT[15:8]));  // open: COut
  and and_1 (INC, CI, not_1_out);
  and and_2 (DEC, CI, INC_DEC);
endmodule

module ALU (
  input  [7:0] A,
  input  [7:0] B,
  input  Carry,
  input  [7:0] OpIn,
  output [7:0] LOutMon,
  output ZF,
  output [7:0] ALU_OUT,
  output Carry_2
);

  wire alu8a_1_cy, multiplexer_1_out, multiplexer_2_out, not_1_out, xor_1_out;
  wire [7:0] alu8a_1_y;

  Multiplexer #(.disabled(0), .enable("false")) multiplexer_1 (
    .in0(1'b0), .in1(Carry), .out(multiplexer_1_out), .sel(OpIn[6]));
  xor xor_1 (xor_1_out, multiplexer_1_out, OpIn[5]);
  ALU8L alu8l_1 (.A(A), .B(B), .S(OpIn[3:0]), .Y(LOutMon));
  // Probe on OpIn[3:0]
  ALU8A alu8a_1 (.B(LOutMon), .A(A), .Cin(xor_1_out), .CY(alu8a_1_cy), .Y(alu8a_1_y));
  SHR shr_1 (.A(LOutMon), .Y(ALU_OUT), .Thru(OpIn[7]), .OE(OpIn[4]));
  assign ALU_OUT = not_1_out ? alu8a_1_y : 8'bz;  // Controlled_Buffer controlled_buffer_1
  not not_1 (not_1_out, OpIn[4]);
  Multiplexer #(.disabled(0), .enable("false")) multiplexer_2 (
    .in0(alu8a_1_cy), .in1(1'b0), .out(multiplexer_2_out), .sel(OpIn[4]));
  ZeroFlag zeroflag_1 (.A(ALU_OUT), .Y(ZF));
  xor xor_2 (Carry_2, multiplexer_2_out, OpIn[5]);

  // Notes on the sheet:
  //   4078
endmodule

module INC_DEC8 (
  input  nThru,
  input  INC_DEC,
  input  CI,
  input  [7:0] A,
  output [7:0] Y,
  output COut
);

  wire and_1_out, and_2_out, and_3_out, and_4_out, and_5_out, and_6_out, and_7_out, and_8_out, and_9_out,
       and_10_out, and_11_out, and_12_out, and_13_out, and_14_out, and_15_out, and_16_out, multiplexer_1_out,
       multiplexer_2_out, multiplexer_3_out, multiplexer_4_out, multiplexer_5_out, multiplexer_6_out,
       multiplexer_7_out, nDEC, Thru;
  wire [7:0] xor_1_out;

  not not_1 (Thru, nThru);
  not not_2 (nDEC, INC_DEC);
  and and_1 (and_1_out, CI, A[0]);
  and and_2 (and_2_out, CI, ~A[0]);  // AND_Gate
  and and_3 (and_3_out, and_1_out, A[1]);
  and and_4 (and_4_out, and_2_out, ~A[1]);  // AND_Gate
  and and_5 (and_5_out, and_3_out, A[2]);
  and and_6 (and_6_out, and_4_out, ~A[2]);  // AND_Gate
  and and_7 (and_7_out, and_5_out, A[3]);
  and and_8 (and_8_out, and_6_out, ~A[3]);  // AND_Gate
  and and_9 (and_9_out, and_7_out, A[4]);
  and and_10 (and_10_out, and_8_out, ~A[4]);  // AND_Gate
  and and_11 (and_11_out, and_9_out, A[5]);
  and and_12 (and_12_out, and_10_out, ~A[5]);  // AND_Gate
  and and_13 (and_13_out, and_11_out, A[6]);
  and and_14 (and_14_out, and_12_out, ~A[6]);  // AND_Gate
  and and_15 (and_15_out, and_13_out, A[7]);
  and and_16 (and_16_out, and_14_out, ~A[7]);  // AND_Gate
  Multiplexer #(.disabled(0), .enable("false")) multiplexer_1 (
    .in0(and_1_out), .in1(and_2_out), .out(multiplexer_1_out), .sel(INC_DEC));
  Multiplexer #(.disabled(0), .enable("false")) multiplexer_2 (
    .in0(and_3_out), .in1(and_4_out), .out(multiplexer_2_out), .sel(INC_DEC));
  Multiplexer #(.disabled(0), .enable("false")) multiplexer_3 (
    .in0(and_5_out), .in1(and_6_out), .out(multiplexer_3_out), .sel(INC_DEC));
  Multiplexer #(.disabled(0), .enable("false")) multiplexer_4 (
    .in0(and_7_out), .in1(and_8_out), .out(multiplexer_4_out), .sel(INC_DEC));
  Multiplexer #(.disabled(0), .enable("false")) multiplexer_5 (
    .in0(and_9_out), .in1(and_10_out), .out(multiplexer_5_out), .sel(INC_DEC));
  Multiplexer #(.disabled(0), .enable("false")) multiplexer_6 (
    .in0(and_11_out), .in1(and_12_out), .out(multiplexer_6_out), .sel(INC_DEC));
  Multiplexer #(.disabled(0), .enable("false")) multiplexer_7 (
    .in0(and_13_out), .in1(and_14_out), .out(multiplexer_7_out), .sel(INC_DEC));
  Multiplexer #(.disabled(0), .enable("false")) multiplexer_8 (
    .in0(and_15_out), .in1(and_16_out), .out(COut), .sel(INC_DEC));
  xor xor_1 (xor_1_out[0], CI, A[0]);
  xor xor_2 (xor_1_out[1], multiplexer_1_out, A[1]);
  xor xor_3 (xor_1_out[2], multiplexer_2_out, A[2]);
  xor xor_4 (xor_1_out[3], multiplexer_3_out, A[3]);
  xor xor_5 (xor_1_out[4], multiplexer_4_out, A[4]);
  xor xor_6 (xor_1_out[5], multiplexer_5_out, A[5]);
  xor xor_7 (xor_1_out[6], multiplexer_6_out, A[6]);
  xor xor_8 (xor_1_out[7], multiplexer_7_out, A[7]);
  Multiplexer #(.width(8), .disabled(0), .enable("false")) multiplexer_9 (
    .in0(xor_1_out), .in1(A), .out(Y), .sel(Thru));

  // Other names for the same wires on the sheet: DEC = INC_DEC
endmodule

module uROM_A_8 (
  input  [7:0] OpeCode,
  input  Load,
  input  Update,
  output [12:0] STEP_MON,
  output [7:0] CtrlSignal
);

  wire not_1_out;

  not not_1 (not_1_out, Load);
  Counter #(.width(5), .max('h1f)) counter_1 (
    .load(Load), .D({5{1'b0}}), .count(not_1_out), .Q(STEP_MON[4:0]), .clk(Update));  // open: carry, clr
  Register _377 (.D(OpeCode), .en(Load), .Q(STEP_MON[12:5]), .clk(Update));  // open: clr
  // Probe on STEP_MON
  ROM #(.addrWidth(13)) rom_1 (.addr(STEP_MON), .data(CtrlSignal));  // open: sel

  // Notes on the sheet:
  //   contents of rom_1 (hex, n*v repeats v):
  //   c 0 c 0 c 0 c 0 c 0 c 0 c 0 c 0 c 0 8c 0 c 0 8c 0 c 0 8c 0 c 0 8c 0 c 1c c 1c c 1c c 1c c 1c c 1c c
  //   1c c 1c c 1c c 1c c 1c c 1c c 1c c 1c c 1c c 1c c 1c c 1c c 1c c 1c c 0 1c 0 c 0 c 0 1c 0 c 0 c 1c c
  //   1c c 1c c 1c c 0 c 0 c 0 c 18*0 80 0 80 0 80 0 80 80 0 80 0 4*c 0 80 0 80 0 80 0 80 0 0 80 0 20 80 0
  //   20 0 80 0 80 0 80 0 80 4*0 8 8 0 0 80 8 8 8 c 1c c c 1c c c 4*15 c 1c c 1c c 1c c 1c 10*0 80 c 0 0
  //   80 0 c 0 1c c 0 1c c 0 c 0 c 1c c 1c c 1c c 1c 4*0 80 33 33 0 80 33 33 80 b3 33 4*0 80 e e 0 80 e e
  //   80 8e e 4*0 80 30 30 0 80 30 30 80 b0 30 4*0 80 c c 0 80 c c 80 8c c 4*0 80 60 60 0 80 60 60 80 e0
  //   60 4*0 80 e e 0 80 e e 80 8e e 4*0 80 58 58 0 80 58 58 80 d8 58 4*0 80 78 78 0 80 78 78 80 f8 78 0
  //   80 70 0 70 80 70 0 80 28 0 28 80 28 0 80 34 0 34 80 34 0 80 35 0 35 80 35 2 82 2 82 2 80 2 1c 1c 3f
  //   bf 3f bf 3f bc 3f 8 8 0 c 1c 12*0 8 c 1c c 1c 1c 7*0 80 f8 0 80 d8 8 8 c 1c 0 0 c 1c c 1c
endmodule

module OP (
  input  [3:0] OPin,
  input  E,
  output [7:0] OpOut,
  output [3:0] OP,
  output FL,
  output nBThru,
  output EXT
);

  wire and_2_out, not_1_out, optable_1_fl;

  OpTable optable_1 (
    .A2(OPin[3]), .A1(OPin[2]), .A0(OPin[1]), .D3(OP[3]), .M(OPin[0]), .D2(OP[2]), .D1(OP[1]), .D0(OP[0]),
    .MO(OpOut[4]), .Ci(OpOut[6]), .FL(optable_1_fl), .CInv(OpOut[5]), .SHR(OpOut[7]));
  not not_1 (not_1_out, optable_1_fl);
  and and_1 (EXT, ~OPin[3], OPin[2], OPin[1], OPin[0]);  // AND_Gate
  and and_2 (and_2_out, OPin[3], ~OPin[2], ~OPin[1], OPin[0]);  // AND_Gate
  and and_3 (FL, not_1_out, E);
  not not_2 (nBThru, and_2_out);

  assign OpOut[3:0] = OP;
endmodule

module OpTable (
  input  A2,
  input  A1,
  input  A0,
  input  M,
  output D3,
  output D2,
  output D1,
  output D0,
  output MO,
  output Ci,
  output FL,
  output CInv,
  output SHR
);

  wire and_1_out, and_2_out, and_3_out, and_4_out, and_5_out, and_6_out, and_7_out, and_8_out, and_9_out,
       and_10_out, and_11_out, and_12_out, and_15_out, and_16_out, and_17_out, and_18_out, and_19_out,
       and_20_out, and_21_out, and_22_out, and_23_out, and_24_out, and_25_out, and_26_out, and_27_out,
       and_28_out, and_29_out, not_1_out, not_2_out, not_3_out, not_4_out, not_5_out, not_6_out, not_7_out,
       not_8_out, not_9_out, not_10_out, not_11_out, not_12_out, not_13_out, not_14_out, not_15_out,
       not_16_out, not_17_out, not_18_out, not_19_out, not_20_out, not_21_out, not_22_out, not_23_out,
       not_24_out, not_25_out, not_26_out, not_27_out, not_28_out, not_29_out, not_30_out, not_31_out,
       not_32_out, not_33_out, not_34_out, not_35_out, not_36_out, not_37_out, not_38_out, not_39_out;

  not not_1 (not_1_out, A1);
  not not_2 (not_2_out, A0);
  and and_1 (and_1_out, not_1_out, not_2_out, M);
  not not_3 (not_3_out, A2);
  and and_2 (and_2_out, not_3_out, A0, not_4_out);
  not not_4 (not_4_out, M);
  and and_3 (and_3_out, A1, A0, M);
  not not_5 (not_5_out, A1);
  and and_4 (and_4_out, A2, not_5_out, not_6_out);
  not not_6 (not_6_out, M);
  and and_5 (and_5_out, A2, not_7_out, not_8_out);
  not not_7 (not_7_out, A0);
  not not_8 (not_8_out, M);
  not not_9 (not_9_out, A2);
  not not_10 (not_10_out, A1);
  not not_11 (not_11_out, A1);
  not not_12 (not_12_out, M);
  not not_13 (not_13_out, A2);
  not not_14 (not_14_out, M);
  not not_15 (not_15_out, A0);
  not not_16 (not_16_out, M);
  not not_17 (not_17_out, A1);
  not not_18 (not_18_out, A0);
  not not_19 (not_19_out, A2);
  not not_20 (not_20_out, A1);
  not not_21 (not_21_out, A0);
  not not_22 (not_22_out, M);
  not not_23 (not_23_out, A2);
  and and_6 (and_6_out, not_23_out, A1, not_24_out);
  not not_24 (not_24_out, M);
  and and_7 (and_7_out, A2, A0, M);
  and and_8 (and_8_out, A2, A1, M);
  not not_25 (not_25_out, A2);
  and and_9 (and_9_out, not_25_out, not_26_out);
  not not_26 (not_26_out, A1);
  not not_27 (not_27_out, A2);
  and and_10 (and_10_out, not_27_out, not_28_out, not_29_out);
  not not_28 (not_28_out, A0);
  not not_29 (not_29_out, M);
  not not_30 (not_30_out, A1);
  and and_11 (and_11_out, not_30_out, not_31_out);
  not not_31 (not_31_out, A0);
  and and_12 (and_12_out, A1, A0, M);
  and and_13 (Ci, A2, A1);
  not not_32 (not_32_out, A1);
  not not_33 (not_33_out, A0);
  not not_34 (not_34_out, M);
  not not_35 (not_35_out, A2);
  not not_36 (not_36_out, A1);
  not not_37 (not_37_out, A0);
  not not_38 (not_38_out, A0);
  not not_39 (not_39_out, A1);
  and and_14 (SHR, A2, A1, A0, M);
  or or_1 (D3, and_1_out, and_2_out, and_3_out, and_4_out, and_5_out);
  and and_15 (and_15_out, not_9_out, not_10_out, A0);
  and and_16 (and_16_out, not_11_out, A0, not_12_out);
  and and_17 (and_17_out, not_13_out, A1, not_14_out);
  and and_18 (and_18_out, A1, not_15_out, not_16_out);
  and and_19 (and_19_out, A2, not_17_out, not_18_out, M);
  and and_20 (and_20_out, A2, A1, A0, M);
  and and_21 (and_21_out, not_19_out, A0);
  and and_22 (and_22_out, A0, M);
  and and_23 (and_23_out, A2, not_20_out, not_21_out, not_22_out);
  and and_24 (and_24_out, A2, A1, M);
  or or_2 (D0, and_6_out, and_7_out, and_8_out);
  or or_3 (MO, and_9_out, and_10_out, and_11_out, and_12_out);
  and and_25 (and_25_out, not_32_out, not_33_out, not_34_out);
  or or_4 (FL, and_25_out, and_26_out, and_27_out);
  and and_26 (and_26_out, not_35_out, A1, A0, M);
  and and_27 (and_27_out, A2, not_36_out, not_37_out);
  and and_28 (and_28_out, A1, not_38_out, M);
  or or_5 (CInv, and_28_out, and_29_out);
  and and_29 (and_29_out, A2, not_39_out, A0, M);
  or or_6 (D2, and_15_out, and_16_out, and_17_out, and_18_out, and_19_out, and_20_out);
  or or_7 (D1, and_21_out, and_22_out, and_23_out, and_24_out);
endmodule

module SHR (
  input  [7:0] A,
  input  Thru,
  input  OE,
  output [7:0] Y
);

  wire not_1_out;
  wire [7:0] multiplexer_1_out;
  wire [7:7] undriven;

  not not_1 (not_1_out, Thru);
  Multiplexer #(.width(8), .disabled(0), .enable("false")) multiplexer_1 (
    .in0({undriven[7], A[7:1]}), .in1(A), .out(multiplexer_1_out), .sel(not_1_out));
  assign Y = OE ? multiplexer_1_out : 8'bz;  // Controlled_Buffer controlled_buffer_1
endmodule

module SXT (
  input  [7:0] A,
  input  Thru,
  input  OE,
  output [7:0] Y
);

  wire not_1_out;
  wire [7:0] multiplexer_1_out;

  not not_1 (not_1_out, Thru);
  Multiplexer #(.width(8), .disabled(0), .enable("false")) multiplexer_1 (
    .in0({8{A[7]}}), .in1(A), .out(multiplexer_1_out), .sel(not_1_out));
  assign Y = OE ? multiplexer_1_out : 8'bz;  // Controlled_Buffer controlled_buffer_1
endmodule

module ALU8L (
  input  [7:0] A,
  input  [7:0] B,
  input  [3:0] S,
  output [7:0] Y
);

  // Probe on S
  Multiplexer #(.select(2), .disabled(0), .enable("false")) multiplexer_1 (
    .in0(S[0]), .in1(S[1]), .in2(S[2]), .in3(S[3]), .out(Y[4]), .sel({B[4], A[4]}));
  Multiplexer #(.select(2), .disabled(0), .enable("false")) multiplexer_2 (
    .in0(S[0]), .in1(S[1]), .in2(S[2]), .in3(S[3]), .out(Y[5]), .sel({B[5], A[5]}));
  Multiplexer #(.select(2), .disabled(0), .enable("false")) multiplexer_3 (
    .in0(S[0]), .in1(S[1]), .in2(S[2]), .in3(S[3]), .out(Y[6]), .sel({B[6], A[6]}));
  Multiplexer #(.select(2), .disabled(0), .enable("false")) multiplexer_4 (
    .in0(S[0]), .in1(S[1]), .in2(S[2]), .in3(S[3]), .out(Y[7]), .sel({B[7], A[7]}));
  Multiplexer #(.select(2), .disabled(0), .enable("false")) multiplexer_5 (
    .in0(S[0]), .in1(S[1]), .in2(S[2]), .in3(S[3]), .out(Y[0]), .sel({B[0], A[0]}));
  Multiplexer #(.select(2), .disabled(0), .enable("false")) multiplexer_6 (
    .in0(S[0]), .in1(S[1]), .in2(S[2]), .in3(S[3]), .out(Y[1]), .sel({B[1], A[1]}));
  Multiplexer #(.select(2), .disabled(0), .enable("false")) multiplexer_7 (
    .in0(S[0]), .in1(S[1]), .in2(S[2]), .in3(S[3]), .out(Y[2]), .sel({B[2], A[2]}));
  Multiplexer #(.select(2), .disabled(0), .enable("false")) multiplexer_8 (
    .in0(S[0]), .in1(S[1]), .in2(S[2]), .in3(S[3]), .out(Y[3]), .sel({B[3], A[3]}));

  // Notes on the sheet:
  //   F16
  //   F16
endmodule

module ALU4A (
  input  [3:0] B,
  input  [3:0] A,
  input  CIn,
  output COut,
  output [3:0] Y
);

  wire and_1_out, and_2_out, and_3_out, and_4_out, and_5_out, and_6_out, and_7_out, and_8_out, and_9_out,
       and_10_out, and_11_out, and_12_out, and_13_out, and_14_out, or_2_out, or_3_out, or_4_out, xor_1_out,
       xor_2_out, xor_3_out, xor_4_out;

  xor xor_1 (xor_1_out, B[3], A[3]);
  and and_1 (and_1_out, B[3], A[3]);
  xor xor_2 (xor_2_out, B[2], A[2]);
  and and_2 (and_2_out, B[2], A[2]);
  xor xor_3 (xor_3_out, B[1], A[1]);
  and and_3 (and_3_out, B[1], A[1]);
  xor xor_4 (xor_4_out, B[0], A[0]);
  and and_4 (and_4_out, B[0], A[0]);
  and and_5 (and_5_out, xor_1_out, and_2_out);
  and and_6 (and_6_out, xor_1_out, xor_2_out, and_3_out);
  and and_7 (and_7_out, xor_1_out, xor_2_out, xor_3_out, and_4_out);
  and and_8 (and_8_out, xor_1_out, xor_2_out, xor_3_out, xor_4_out, CIn);
  and and_9 (and_9_out, xor_2_out, and_3_out);
  and and_10 (and_10_out, xor_2_out, xor_3_out, and_4_out);
  and and_11 (and_11_out, xor_2_out, xor_3_out, xor_4_out, CIn);
  and and_12 (and_12_out, xor_3_out, and_4_out);
  and and_13 (and_13_out, xor_3_out, xor_4_out, CIn);
  and and_14 (and_14_out, xor_4_out, CIn);
  or or_1 (COut, and_1_out, and_5_out, and_6_out, and_7_out, and_8_out);
  or or_2 (or_2_out, and_2_out, and_9_out, and_10_out, and_11_out);
  or or_3 (or_3_out, and_3_out, and_12_out, and_13_out);
  or or_4 (or_4_out, and_4_out, and_14_out);
  xor xor_5 (Y[3], xor_1_out, or_2_out);
  xor xor_6 (Y[2], xor_2_out, or_3_out);
  xor xor_7 (Y[1], xor_3_out, or_4_out);
  xor xor_8 (Y[0], xor_4_out, CIn);
endmodule

module ALU8A (
  input  [7:0] B,
  input  [7:0] A,
  input  Cin,
  output CY,
  output [7:0] Y
);

  wire alu4a_2_cout;

  ALU4A alu4a_1 (.B(B[7:4]), .A(A[7:4]), .CIn(alu4a_2_cout), .COut(CY), .Y(Y[7:4]));
  ALU4A alu4a_2 (.B(B[3:0]), .A(A[3:0]), .CIn(Cin), .COut(alu4a_2_cout), .Y(Y[3:0]));
endmodule

module ZeroFlag (
  input  [7:0] A,
  output Y
);

  nor nor_1 (Y, A[0], A[1], A[2], A[3], A[4], A[5], A[6], A[7]);
endmodule

module MUX4to1x8 (
  input  [7:0] D0,
  input  [7:0] D1,
  input  [7:0] D2,
  input  [7:0] D3,
  input  [1:0] Sel,
  output [7:0] Y,
  output I0,
  output I1,
  output I2,
  output I3
);

  Multiplexer #(.select(2), .width(8), .enable("false")) multiplexer_1 (
    .in0(D0), .in1(D1), .in2(D2), .in3(D3), .out(Y), .sel(Sel));
  Demultiplexer #(.select(2), .disabled(0), .enable("false")) demultiplexer_1 (
    .out0(I0), .out1(I1), .out2(I2), .out3(I3), .in(1'b1), .sel(Sel));

  // Notes on the sheet:
  //   139
endmodule

module MUX4to1x16 (
  input  [15:0] D0,
  input  [15:0] D1,
  input  [15:0] D2,
  input  [15:0] D3,
  input  [1:0] Sel,
  output [15:0] Y,
  output I0,
  output I1,
  output I2,
  output I3
);

  Multiplexer #(.select(2), .width(16), .enable("false")) multiplexer_1 (
    .in0(D0), .in1(D1), .in2(D2), .in3(D3), .out(Y), .sel(Sel));
  Demultiplexer #(.select(2), .disabled(0), .enable("false")) demultiplexer_1 (
    .out0(I0), .out1(I1), .out2(I2), .out3(I3), .in(1'b1), .sel(Sel));

  // Notes on the sheet:
  //   139
endmodule

module Equal14 (
  input  [13:0] In0,
  input  [13:0] In1,
  output Y
);

  wire [13:0] not_1_out, xor_1_out;

  assign not_1_out = ~xor_1_out;  // NOT_Gate not_1, 14 bits wide
  assign xor_1_out = In0 ^ In1;  // XOR_Gate xor_1, 14 bits wide
  and and_1 (Y, not_1_out[0], not_1_out[1], not_1_out[2], not_1_out[3], not_1_out[4], not_1_out[5], not_1_out[6], not_1_out[7], not_1_out[8], not_1_out[9], not_1_out[10], not_1_out[11], not_1_out[12], not_1_out[13]);
endmodule
