// Logisim project CPU298_parts_placement.circ as structural Verilog
module main_board (
);

  DIP14 HC04 ();  // open: in_2, in_3, in_4, in_5, in_6, in_7, in_8, out_9, out_10, out_11, out_12, out_13, out_14, in_1
  DIP20 dip20_1 ();  // open: in_1, in_2, in_3, in_4, in_5, in_6, in_7, in_8, in_9, in_10, out_11, out_12, out_13, out_14, out_15, out_16, out_17, out_18, out_19, out_20
  DIP16 dip16_1 ();  // open: in_1, in_2, in_3, in_4, in_5, in_6, in_7, in_8, out_9, out_10, out_11, out_12, out_13, out_14, out_15, out_16
  DIP24 ATF22 ();  // open: in_1, in_2, in_3, in_4, in_5, in_6, in_7, in_8, in_9, in_10, in_11, in_12, out_13, out_14, out_15, out_16, out_17, out_18, out_19, out_20, out_21, out_22, out_23, out_24
  DIP14 HC00 ();  // open: in_2, in_3, in_4, in_5, in_6, in_7, in_8, out_9, out_10, out_11, out_12, out_13, out_14, in_1
  _40pinSocket u_40pinsocket_1 ();
endmodule

module DIP14 (
  input  in_1,
  input  in_2,
  input  in_3,
  input  in_4,
  input  in_5,
  input  in_6,
  input  in_7,
  input  in_8,
  output out_9,
  output out_10,
  output out_11,
  output out_12,
  output out_13,
  output out_14
);


  assign out_9 = in_2;
  assign out_10 = in_3;
  assign out_11 = in_4;
  assign out_12 = in_5;
  assign out_13 = in_6;
  assign out_14 = in_7;
endmodule

module DIP16 (
  input  in_1,
  input  in_2,
  input  in_3,
  input  in_4,
  input  in_5,
  input  in_6,
  input  in_7,
  input  in_8,
  output out_9,
  output out_10,
  output out_11,
  output out_12,
  output out_13,
  output out_14,
  output out_15,
  output out_16
);


  assign out_9 = in_1;
  assign out_10 = in_2;
  assign out_11 = in_3;
  assign out_12 = in_4;
  assign out_13 = in_5;
  assign out_14 = in_6;
  assign out_15 = in_7;
  assign out_16 = in_8;
endmodule

module DIP20 (
  input  in_1,
  input  in_2,
  input  in_3,
  input  in_4,
  input  in_5,
  input  in_6,
  input  in_7,
  input  in_8,
  input  in_9,
  input  in_10,
  output out_11,
  output out_12,
  output out_13,
  output out_14,
  output out_15,
  output out_16,
  output out_17,
  output out_18,
  output out_19,
  output out_20
);


  assign out_12 = in_1;
  assign out_13 = in_2;
  assign out_14 = in_3;
  assign out_15 = in_4;
  assign out_16 = in_5;
  assign out_17 = in_6;
  assign out_18 = in_7;
  assign out_19 = in_8;
  assign out_20 = in_9;
endmodule

module DIP24 (
  input  in_1,
  input  in_2,
  input  in_3,
  input  in_4,
  input  in_5,
  input  in_6,
  input  in_7,
  input  in_8,
  input  in_9,
  input  in_10,
  input  in_11,
  input  in_12,
  output out_13,
  output out_14,
  output out_15,
  output out_16,
  output out_17,
  output out_18,
  output out_19,
  output out_20,
  output out_21,
  output out_22,
  output out_23,
  output out_24
);


  assign out_14 = in_1;
  assign out_15 = in_2;
  assign out_16 = in_3;
  assign out_17 = in_4;
  assign out_18 = in_5;
  assign out_19 = in_6;
  assign out_20 = in_7;
  assign out_21 = in_8;
  assign out_22 = in_9;
  assign out_23 = in_10;
  assign out_24 = in_11;
endmodule
