// Logisim project TD4-Yoshi.circ as structural Verilog: 2 circuits, main circuit main
module main (
);

  wire and_1_out, CLK, CY_qn, n6116_1__14__i_o4, n74173_3__3___1q, n74173_3__4___2q, n74173_3__5___3q,
       n74173_3__6___4q, n74259_1__4__q0, n74259_1__5__q1, n74259_1__6__q2, n74259_1__7__q3, n74259_1__9__q4,
       n74259_1__10__q5, n74259_1__11__q6, n74259_1__12__q7, n74283_1__9__cout, nCLK, nor_1_out, nRST,
       or_1_out, PCH_p4, PCH_p10, PCL_p7, RST;
  wire [0:0] nor_2_out, or_2_out;
  wire [1:0] n6116_1__16__i_o6, not_3_out;
  wire [1:1] nand_3_out;
  wire [3:0] n6116_1__9__i_o0, n74283_1__4__s1, pull_resistor_1_node, pull_resistor_2_node;
  wire [4:0] PCL_p8;

  Button button_1 (.out(RST));
  Clock clock_1 (.out(CLK));
  LED led_1 (.in(n74259_1__12__q7));
  LED led_2 (.in(n74259_1__11__q6));
  LED led_3 (.in(n74259_1__10__q5));
  LED led_4 (.in(n74259_1__9__q4));
  LED led_5 (.in(n74259_1__7__q3));
  LED led_6 (.in(n74259_1__6__q2));
  LED led_7 (.in(n74259_1__5__q1));
  LED led_8 (.in(n74259_1__4__q0));
  not not_1 (nRST, RST);
  not not_2 (nCLK, CLK);
  _74259 u_74259_1 (
    ._1__S0(n74173_3__3___1q), ._2__S1(n74173_3__4___2q), ._3__S2(n74173_3__5___3q),
    ._4__Q0(n74259_1__4__q0), ._5__Q1(n74259_1__5__q1), ._6__Q2(n74259_1__6__q2), ._7__Q3(n74259_1__7__q3),
    ._15__CLR(nRST), ._14__G(nCLK), ._13__D(n74173_3__6___4q), ._12__Q7(n74259_1__12__q7),
    ._11__Q6(n74259_1__11__q6), ._10__Q5(n74259_1__10__q5), ._9__Q4(n74259_1__9__q4));  // open: _8__GND, _16__Vcc
  Pull_Resistor pull_resistor_1 (.node(pull_resistor_1_node));
  Button button_2 (.out(pull_resistor_2_node[3]));
  // Probe on pull_resistor_1_node
  _74173 u_74173_1 (
    ._1____M(or_2_out[0]), ._2____N(not_3_out[1]), ._3___1Q(pull_resistor_1_node[0]),
    ._4___2Q(pull_resistor_1_node[1]), ._5___3Q(pull_resistor_1_node[2]), ._6___4Q(pull_resistor_1_node[3]),
    ._7__CLK(CLK), ._15_CLR(RST), ._14__1D(n74283_1__4__s1[0]), ._13___2D(n74283_1__4__s1[1]),
    ._12___3D(n74283_1__4__s1[2]), ._11___4D(n74283_1__4__s1[3]), ._10___2G(n6116_1__16__i_o6[0]),
    ._9___1G(n6116_1__16__i_o6[1]));  // open: _8__GND, _16__Vcc
  _74173 u_74173_2 (
    ._1____M(not_3_out[0]), ._2____N(not_3_out[1]), ._3___1Q(pull_resistor_1_node[0]),
    ._4___2Q(pull_resistor_1_node[1]), ._5___3Q(pull_resistor_1_node[2]), ._6___4Q(pull_resistor_1_node[3]),
    ._7__CLK(CLK), ._15_CLR(RST), ._14__1D(n74283_1__4__s1[0]), ._13___2D(n74283_1__4__s1[1]),
    ._12___3D(n74283_1__4__s1[2]), ._11___4D(n74283_1__4__s1[3]), ._10___2G(nor_2_out[0]),
    ._9___1G(n6116_1__16__i_o6[1]));  // open: _8__GND, _16__Vcc
  _74173 u_74173_3 (
    ._1____M(1'b0), ._2____N(1'b0), ._3___1Q(n74173_3__3___1q), ._4___2Q(n74173_3__4___2q),
    ._5___3Q(n74173_3__5___3q), ._6___4Q(n74173_3__6___4q), ._7__CLK(CLK), ._15_CLR(RST),
    ._14__1D(n74283_1__4__s1[0]), ._13___2D(n74283_1__4__s1[1]), ._12___3D(n74283_1__4__s1[2]),
    ._11___4D(n74283_1__4__s1[3]), ._10___2G(n6116_1__16__i_o6[0]), ._9___1G(nand_3_out[1]));  // open: _8__GND, _16__Vcc
  _74173 u_74173_4 (
    ._1____M(PCH_p4), ._2____N(PCH_p4), ._3___1Q(pull_resistor_1_node[0]), ._4___2Q(pull_resistor_1_node[1]),
    ._5___3Q(pull_resistor_1_node[2]), ._6___4Q(pull_resistor_1_node[3]), ._7__CLK(nCLK),
    ._15_CLR(or_2_out[0]), ._14__1D(pull_resistor_2_node[0]), ._13___2D(pull_resistor_2_node[1]),
    ._12___3D(pull_resistor_2_node[2]), ._11___4D(pull_resistor_2_node[3]), ._10___2G(1'b0), ._9___1G(1'b0));  // open: _8__GND, _16__Vcc
  Button button_3 (.out(pull_resistor_2_node[1]));
  Button button_4 (.out(pull_resistor_2_node[2]));
  // Probe on n74283_1__4__s1
  Pull_Resistor pull_resistor_2 (.node(pull_resistor_2_node));
  Button button_5 (.out(pull_resistor_2_node[0]));
  _74283 u_74283_1 (
    ._1__S2(n74283_1__4__s1[1]), ._2__B2(n6116_1__9__i_o0[1]), ._3__A2(pull_resistor_1_node[1]),
    ._4__S1(n74283_1__4__s1[0]), ._5__A1(pull_resistor_1_node[0]), ._6__B1(n6116_1__9__i_o0[0]),
    ._7__Cin(1'b0), ._15__B3(n6116_1__9__i_o0[2]), ._14__A3(pull_resistor_1_node[2]),
    ._13__S3(n74283_1__4__s1[2]), ._12__A4(pull_resistor_1_node[3]), ._11__B4(n6116_1__9__i_o0[3]),
    ._10__S4(n74283_1__4__s1[3]), ._9__Cout(n74283_1__9__cout));  // open: _8__GND, _16__Vcc
  // _74161 PCL: pin names not known; wires that end beside it: nRST, CLK, n74283_1__4__s1[0], n74283_1__4__s1[1], n74283_1__4__s1[2], n74283_1__4__s1[3], PCL_p7, PCL_p8[0], PCL_p8[1], PCL_p8[2], PCL_p8[3]
  // _74161 PCH: pin names not known; wires that end beside it: 1'b1, nRST, CLK, PCH_p4, 1'b0, 1'b0, 1'b0, 1'b1, 1'b1, PCH_p10, PCL_p8[4], PCL_p7, PCH_p10
  // Probe on PCL_p8
  // Probe on n6116_1__9__i_o0
  or or_1 (or_1_out, ~CY_qn, ~nor_1_out);  // OR_Gate
  nand nand_1 (PCH_p10, or_1_out, and_1_out);
  and and_1 (and_1_out, ~nor_2_out[0], ~nand_3_out[1]);  // AND_Gate
  nor nor_1 (nor_1_out, n6116_1__14__i_o4, n6116_1__14__i_o4);
  D_Flip_Flop CY (.clk(CLK), .D(n74283_1__9__cout), .Qn(CY_qn), .preset(1'b0), .reset(RST));  // open: Q, en
  _6116 u_6116_1 (
    ._1__A7(1'b0), ._2__A6(1'b0), ._3__A5(1'b0), ._4__A4(PCL_p8[4]), ._5__A3(PCL_p8[3]), ._6__A2(PCL_p8[2]),
    ._7__A1(PCL_p8[1]), ._8__A0(PCL_p8[0]), ._9__I_O0(n6116_1__9__i_o0[0]), ._10__I_O1(n6116_1__9__i_o0[1]),
    ._11__I_O2(n6116_1__9__i_o0[2]), ._23__A8(1'b0), ._22__A9(1'b0), ._21___WE(1'b1), ._20___OE(1'b0),
    ._19__A10(1'b0), ._18___CS(1'b0), ._17__I_O7(n6116_1__16__i_o6[1]), ._16__I_O6(n6116_1__16__i_o6[0]),
    ._15__I_O5(not_3_out[1]), ._14__I_O4(n6116_1__14__i_o4), ._13__I_O3(n6116_1__9__i_o0[3]));  // open: _12__GND, _24__Vcc
  nor nor_2 (nor_2_out[0], n6116_1__16__i_o6[0], n6116_1__16__i_o6[0]);
  nand nand_2 (PCH_p4, not_3_out[1], not_3_out[1]);
  nand nand_3 (nand_3_out[1], n6116_1__16__i_o6[1], n6116_1__16__i_o6[1]);
  or or_2 (or_2_out[0], ~nand_3_out[1], ~nor_1_out);  // OR_Gate
  not not_3 (not_3_out[0], or_2_out[0]);

  // Notes on the sheet:
  //   RST
  //   CLK
  //   RegO G1
  //   RegO G2
  //   RegB G1
  //   RegB G2
  //   RegA G1
  //   RegA G2
  //   RegA M
  //   RegA N
  //   RegB M
  //   RegB N
endmodule

module _6116 (
  input  _1__A7,
  input  _24__Vcc,
  input  _2__A6,
  input  _23__A8,
  input  _3__A5,
  input  _22__A9,
  input  _4__A4,
  input  _21___WE,
  input  _5__A3,
  input  _20___OE,
  input  _6__A2,
  input  _19__A10,
  input  _7__A1,
  input  _18___CS,
  input  _8__A0,
  input  _12__GND,
  output _17__I_O7,
  output _9__I_O0,
  output _16__I_O6,
  output _10__I_O1,
  output _15__I_O5,
  output _11__I_O2,
  output _14__I_O4,
  output _13__I_O3
);

  wire and_1_out, and_2_out, not_1_out, not_2_out;
  wire [7:0] controlled_buffer_1_out;

  assign controlled_buffer_1_out = and_2_out ? {_17__I_O7, _16__I_O6, _15__I_O5, _14__I_O4, _13__I_O3, _11__I_O2, _10__I_O1, _9__I_O0} : 8'bz;  // Controlled_Buffer controlled_buffer_1
  not not_1 (not_1_out, _18___CS);
  and and_1 (and_1_out, ~_20___OE, ~_18___CS, _21___WE);  // AND_Gate
  assign {_17__I_O7, _16__I_O6, _15__I_O5, _14__I_O4, _13__I_O3, _11__I_O2, _10__I_O1, _9__I_O0} = and_1_out ? controlled_buffer_1_out : 8'bz;  // Controlled_Buffer controlled_buffer_2
  and and_2 (and_2_out, ~_18___CS, ~_21___WE);  // AND_Gate
  RAM #(.addrWidth(11), .bus("asynch")) ram_1 (
    .addr({_19__A10, _22__A9, _23__A8, _1__A7, _2__A6, _3__A5, _4__A4, _5__A3, _6__A2, _7__A1, _8__A0}),
    .data(controlled_buffer_1_out), .sel(not_1_out), .ld(not_2_out));  // open: clr
  not not_2 (not_2_out, and_2_out);
endmodule
